// Logisim project 8bit_computer.circ as structural Verilog: 36 circuits, main circuit main
module main (
);


  // Notes on the sheet:
  //   Final design is under "Computer", the last circuit in the project.
endmodule

module Register_8bit (
  input  [7:0] I,
  input  Enable,
  input  CLK,
  input  CLR,
  output [7:0] O
);

  wire multiplexer_1_out, multiplexer_2_out, multiplexer_3_out, multiplexer_4_out, multiplexer_5_out,
       multiplexer_6_out, multiplexer_7_out, multiplexer_8_out;

  Multiplexer multiplexer_1 (.in0(O[0]), .in1(I[0]), .out(multiplexer_1_out), .sel(Enable));
  Multiplexer multiplexer_2 (.in0(O[1]), .in1(I[1]), .out(multiplexer_2_out), .sel(Enable));
  Multiplexer multiplexer_3 (.in0(O[2]), .in1(I[2]), .out(multiplexer_3_out), .sel(Enable));
  Multiplexer multiplexer_4 (.in0(O[3]), .in1(I[3]), .out(multiplexer_4_out), .sel(Enable));
  Multiplexer multiplexer_5 (.in0(O[4]), .in1(I[4]), .out(multiplexer_5_out), .sel(Enable));
  Multiplexer multiplexer_6 (.in0(O[5]), .in1(I[5]), .out(multiplexer_6_out), .sel(Enable));
  Multiplexer multiplexer_7 (.in0(O[6]), .in1(I[6]), .out(multiplexer_7_out), .sel(Enable));
  Multiplexer multiplexer_8 (.in0(O[7]), .in1(I[7]), .out(multiplexer_8_out), .sel(Enable));
  D_Flip_Flop d_ff_1 (.D(multiplexer_1_out), .clk(CLK), .Q(O[0]), .reset(CLR));  // open: Qn, preset
  D_Flip_Flop d_ff_2 (.D(multiplexer_2_out), .clk(CLK), .Q(O[1]), .reset(CLR));  // open: Qn, preset
  D_Flip_Flop d_ff_3 (.D(multiplexer_3_out), .clk(CLK), .Q(O[2]), .reset(CLR));  // open: Qn, preset
  D_Flip_Flop d_ff_4 (.D(multiplexer_4_out), .clk(CLK), .Q(O[3]), .reset(CLR));  // open: Qn, preset
  D_Flip_Flop d_ff_5 (.D(multiplexer_5_out), .clk(CLK), .Q(O[4]), .reset(CLR));  // open: Qn, preset
  D_Flip_Flop d_ff_6 (.D(multiplexer_6_out), .clk(CLK), .Q(O[5]), .reset(CLR));  // open: Qn, preset
  D_Flip_Flop d_ff_7 (.D(multiplexer_7_out), .clk(CLK), .Q(O[6]), .reset(CLR));  // open: Qn, preset
  D_Flip_Flop d_ff_8 (.D(multiplexer_8_out), .clk(CLK), .Q(O[7]), .reset(CLR));  // open: Qn, preset

  // Other names for the same wires on the sheet: Q0 = O[0]; Q1 = O[1]; Q2 = O[2]; Q3 = O[3]; Q4 = O[4]; Q5 = O[5];
  //   Q6 = O[6]; Q7 = O[7]
endmodule

module Three_State_Output_8bits (
  input  [7:0] I,
  input  EN,
  output [7:0] O
);

  assign O[0] = EN ? I[0] : 1'bz;  // Controlled_Buffer controlled_buffer_1
  assign O[1] = EN ? I[1] : 1'bz;  // Controlled_Buffer controlled_buffer_2
  assign O[2] = EN ? I[2] : 1'bz;  // Controlled_Buffer controlled_buffer_3
  assign O[3] = EN ? I[3] : 1'bz;  // Controlled_Buffer controlled_buffer_4
  assign O[4] = EN ? I[4] : 1'bz;  // Controlled_Buffer controlled_buffer_5
  assign O[5] = EN ? I[5] : 1'bz;  // Controlled_Buffer controlled_buffer_6
  assign O[6] = EN ? I[6] : 1'bz;  // Controlled_Buffer controlled_buffer_7
  assign O[7] = EN ? I[7] : 1'bz;  // Controlled_Buffer controlled_buffer_8
endmodule

module Register_8bit_Three_State_Output (
  input  [7:0] I,
  input  CLR,
  input  CLK,
  input  EN_I,
  input  EN_O,
  output [7:0] O
);

  wire [7:0] register_8bit_1_o;

  Register_8bit register_8bit_1 (.O(register_8bit_1_o), .I(I), .Enable(EN_I), .CLK(CLK), .CLR(CLR));
  Three_State_Output_8bits three_state_output_8bits_1 (.O(O), .I(register_8bit_1_o), .EN(EN_O));
endmodule

module AND_8bit (
  input  [7:0] A,
  input  [7:0] B,
  output [7:0] O
);

  and and_1 (O[0], A[0], B[0]);
  and and_2 (O[1], A[1], B[1]);
  and and_3 (O[2], A[2], B[2]);
  and and_4 (O[3], A[3], B[3]);
  and and_5 (O[4], A[4], B[4]);
  and and_6 (O[5], A[5], B[5]);
  and and_7 (O[6], A[6], B[6]);
  and and_8 (O[7], A[7], B[7]);
endmodule

module OR_8bit (
  input  [7:0] A,
  input  [7:0] B,
  output [7:0] O
);

  or or_1 (O[0], A[0], B[0]);
  or or_2 (O[1], A[1], B[1]);
  or or_3 (O[2], A[2], B[2]);
  or or_4 (O[3], A[3], B[3]);
  or or_5 (O[4], A[4], B[4]);
  or or_6 (O[5], A[5], B[5]);
  or or_7 (O[6], A[6], B[6]);
  or or_8 (O[7], A[7], B[7]);
endmodule

module NAND_8bit (
  input  [7:0] A,
  input  [7:0] B,
  output [7:0] O
);

  nand nand_1 (O[0], A[0], B[0]);
  nand nand_2 (O[1], A[1], B[1]);
  nand nand_3 (O[2], A[2], B[2]);
  nand nand_4 (O[3], A[3], B[3]);
  nand nand_5 (O[4], A[4], B[4]);
  nand nand_6 (O[5], A[5], B[5]);
  nand nand_7 (O[6], A[6], B[6]);
  nand nand_8 (O[7], A[7], B[7]);
endmodule

module NOR_8bit (
  input  [7:0] A,
  input  [7:0] B,
  output [7:0] O
);

  nor nor_1 (O[0], A[0], B[0]);
  nor nor_2 (O[1], A[1], B[1]);
  nor nor_3 (O[2], A[2], B[2]);
  nor nor_4 (O[3], A[3], B[3]);
  nor nor_5 (O[4], A[4], B[4]);
  nor nor_6 (O[5], A[5], B[5]);
  nor nor_7 (O[6], A[6], B[6]);
  nor nor_8 (O[7], A[7], B[7]);
endmodule

module XOR_8bit (
  input  [7:0] A,
  input  [7:0] B,
  output [7:0] O
);

  xor xor_1 (O[0], A[0], B[0]);
  xor xor_2 (O[1], A[1], B[1]);
  xor xor_3 (O[2], A[2], B[2]);
  xor xor_4 (O[3], A[3], B[3]);
  xor xor_5 (O[4], A[4], B[4]);
  xor xor_6 (O[5], A[5], B[5]);
  xor xor_7 (O[6], A[6], B[6]);
  xor xor_8 (O[7], A[7], B[7]);
endmodule

module XNOR_8bit (
  input  [7:0] A,
  input  [7:0] B,
  output [7:0] O
);

  xnor xnor_1 (O[0], A[0], B[0]);
  xnor xnor_2 (O[1], A[1], B[1]);
  xnor xnor_3 (O[2], A[2], B[2]);
  xnor xnor_4 (O[3], A[3], B[3]);
  xnor xnor_5 (O[4], A[4], B[4]);
  xnor xnor_6 (O[5], A[5], B[5]);
  xnor xnor_7 (O[6], A[6], B[6]);
  xnor xnor_8 (O[7], A[7], B[7]);
endmodule

module Complement (
  input  [7:0] A,
  output [7:0] O
);

  not not_1 (O[0], A[0]);
  not not_2 (O[1], A[1]);
  not not_3 (O[2], A[2]);
  not not_4 (O[3], A[3]);
  not not_5 (O[4], A[4]);
  not not_6 (O[5], A[5]);
  not not_7 (O[6], A[6]);
  not not_8 (O[7], A[7]);
endmodule

module Adder_1bit (
  input  A,
  input  B,
  input  Cin,
  output Sum,
  output Cout
);

  wire and_1_out, and_2_out, xor_1_out;

  xor xor_1 (xor_1_out, A, B);
  and and_1 (and_1_out, xor_1_out, Cin);
  and and_2 (and_2_out, A, B);
  xor xor_2 (Sum, xor_1_out, Cin);
  or or_1 (Cout, and_1_out, and_2_out);
endmodule

module Adder_8bit (
  input  B7,
  input  A7,
  input  B6,
  input  A6,
  input  B5,
  input  A5,
  input  B4,
  input  A4,
  input  B3,
  input  A3,
  input  B2,
  input  A2,
  input  B1,
  input  A1,
  input  B0,
  input  A0,
  input  Cin,
  output Cout,
  output Output7,
  output Output6,
  output Output5,
  output Output4,
  output Output3,
  output Output2,
  output Output1,
  output Output0
);

  wire adder_1bit_2_cout, adder_1bit_3_cout, adder_1bit_4_cout, adder_1bit_5_cout, adder_1bit_6_cout,
       adder_1bit_7_cout, adder_1bit_8_cout;

  Adder_1bit adder_1bit_1 (.Sum(Output7), .Cout(Cout), .A(A7), .B(B7), .Cin(adder_1bit_2_cout));
  Adder_1bit adder_1bit_2 (.Sum(Output6), .Cout(adder_1bit_2_cout), .A(A6), .B(B6), .Cin(adder_1bit_3_cout));
  Adder_1bit adder_1bit_3 (.Sum(Output5), .Cout(adder_1bit_3_cout), .A(A5), .B(B5), .Cin(adder_1bit_4_cout));
  Adder_1bit adder_1bit_4 (.Sum(Output4), .Cout(adder_1bit_4_cout), .A(A4), .B(B4), .Cin(adder_1bit_5_cout));
  Adder_1bit adder_1bit_5 (.Sum(Output3), .Cout(adder_1bit_5_cout), .A(A3), .B(B3), .Cin(adder_1bit_6_cout));
  Adder_1bit adder_1bit_6 (.Sum(Output2), .Cout(adder_1bit_6_cout), .A(A2), .B(B2), .Cin(adder_1bit_7_cout));
  Adder_1bit adder_1bit_7 (.Sum(Output1), .Cout(adder_1bit_7_cout), .A(A1), .B(B1), .Cin(adder_1bit_8_cout));
  Adder_1bit adder_1bit_8 (.Sum(Output0), .Cout(adder_1bit_8_cout), .A(A0), .B(B0), .Cin(Cin));
endmodule

module Adder_Subtractor_8bit (
  input  [7:0] A,
  input  Cin,
  input  [7:0] B,
  input  Sub,
  output [7:0] Sum_Subtraction,
  output Cout
);

  wire B0, B1, B2, B3, B4, B5, B6, B7;

  xor xor_1 (B0, B[0], Sub);
  xor xor_2 (B1, B[1], Sub);
  xor xor_3 (B2, B[2], Sub);
  xor xor_4 (B3, B[3], Sub);
  xor xor_5 (B4, B[4], Sub);
  xor xor_6 (B5, B[5], Sub);
  xor xor_7 (B6, B[6], Sub);
  xor xor_8 (B7, B[7], Sub);
  Adder_8bit adder_8bit_1 (
    .Output2(Sum_Subtraction[2]), .Output1(Sum_Subtraction[1]), .Output0(Sum_Subtraction[0]), .Cout(Cout),
    .Output7(Sum_Subtraction[7]), .Output6(Sum_Subtraction[6]), .Output5(Sum_Subtraction[5]),
    .Output4(Sum_Subtraction[4]), .Output3(Sum_Subtraction[3]), .A2(A[2]), .B1(B1), .A1(A[1]), .B0(B0),
    .Cin(Cin), .A0(A[0]), .B7(B7), .A7(A[7]), .B6(B6), .A6(A[6]), .B5(B5), .A5(A[5]), .B4(B4), .A4(A[4]),
    .B3(B3), .A3(A[3]), .B2(B2));
endmodule

module Shift_Left_Right_Rotate_Left_Right (
  input  [7:0] A,
  input  [1:0] S,
  output [7:0] O,
  output Cout
);

  wire and_1_out, and_2_out, and_3_out, and_4_out, not_1_out, not_2_out;

  Multiplexer #(.select(2)) multiplexer_1 (.in0(1'b0), .in1(A[1]), .in2(A[7]), .in3(A[1]), .out(O[0]), .sel(S));
  Multiplexer #(.select(2)) multiplexer_2 (.in0(A[0]), .in1(A[2]), .in2(A[0]), .in3(A[2]), .out(O[1]), .sel(S));
  Multiplexer #(.select(2)) multiplexer_3 (.in0(A[1]), .in1(A[3]), .in2(A[1]), .in3(A[3]), .out(O[2]), .sel(S));
  Multiplexer #(.select(2)) multiplexer_4 (.in0(A[2]), .in1(A[4]), .in2(A[2]), .in3(A[4]), .out(O[3]), .sel(S));
  Multiplexer #(.select(2)) multiplexer_5 (.in0(A[3]), .in1(A[5]), .in2(A[3]), .in3(A[5]), .out(O[4]), .sel(S));
  Multiplexer #(.select(2)) multiplexer_6 (.in0(A[4]), .in1(A[6]), .in2(A[4]), .in3(A[6]), .out(O[5]), .sel(S));
  Multiplexer #(.select(2)) multiplexer_7 (.in0(A[5]), .in1(A[7]), .in2(A[5]), .in3(A[7]), .out(O[6]), .sel(S));
  Multiplexer #(.select(2)) multiplexer_8 (.in0(A[6]), .in1(1'b0), .in2(A[6]), .in3(A[0]), .out(O[7]), .sel(S));
  not not_1 (not_1_out, S[0]);
  not not_2 (not_2_out, S[1]);
  and and_1 (and_1_out, not_1_out, not_2_out);
  and and_2 (and_2_out, not_2_out, S[0]);
  and and_3 (and_3_out, A[7], and_1_out);
  and and_4 (and_4_out, and_2_out, A[0]);
  or or_1 (Cout, and_3_out, and_4_out);
endmodule

module Multiplier_4bits (
  input  [7:0] A,
  output [7:0] O
);

  wire adder_8bit_1_output1, adder_8bit_1_output2, adder_8bit_1_output3, adder_8bit_1_output4,
       adder_8bit_2_output1, adder_8bit_2_output2, adder_8bit_2_output3, adder_8bit_2_output4, O1_1, O1_2,
       O1_3, O2_0, O2_1, O2_2, O2_3, O3_0, O3_1, O3_2, O3_3, O4_0, O4_1, O4_2, O4_3;

  and and_1 (O[0], A[4], A[0]);
  and and_2 (O1_1, A[5], A[0]);
  and and_3 (O1_2, A[6], A[0]);
  and and_4 (O1_3, A[7], A[0]);
  and and_5 (O2_0, A[4], A[1]);
  and and_6 (O2_1, A[5], A[1]);
  and and_7 (O2_2, A[6], A[1]);
  and and_8 (O2_3, A[7], A[1]);
  and and_9 (O3_0, A[4], A[2]);
  and and_10 (O3_1, A[5], A[2]);
  and and_11 (O3_2, A[6], A[2]);
  and and_12 (O3_3, A[7], A[2]);
  and and_13 (O4_0, A[4], A[3]);
  and and_14 (O4_1, A[5], A[3]);
  and and_15 (O4_2, A[6], A[3]);
  and and_16 (O4_3, A[7], A[3]);
  Adder_8bit adder_8bit_1 (
    .Output2(adder_8bit_1_output2), .Output1(adder_8bit_1_output1), .Output0(O[1]),
    .Output4(adder_8bit_1_output4), .Output3(adder_8bit_1_output3), .A2(O1_3), .B1(O2_1), .A1(O1_2),
    .B0(O2_0), .Cin(1'b0), .A0(O1_1), .B7(1'b0), .A7(1'b0), .B6(1'b0), .A6(1'b0), .B5(1'b0), .A5(1'b0),
    .B4(1'b0), .A4(1'b0), .B3(O2_3), .A3(1'b0), .B2(O2_2));  // open: Cout, Output7, Output6, Output5
  Adder_8bit adder_8bit_2 (
    .Output2(adder_8bit_2_output2), .Output1(adder_8bit_2_output1), .Output0(O[2]),
    .Output4(adder_8bit_2_output4), .Output3(adder_8bit_2_output3), .A2(adder_8bit_1_output3), .B1(O3_1),
    .A1(adder_8bit_1_output2), .B0(O3_0), .Cin(1'b0), .A0(adder_8bit_1_output1), .B7(1'b0), .A7(1'b0),
    .B6(1'b0), .A6(1'b0), .B5(1'b0), .A5(1'b0), .B4(1'b0), .A4(1'b0), .B3(O3_3), .A3(adder_8bit_1_output4),
    .B2(O3_2));  // open: Cout, Output7, Output6, Output5
  Adder_8bit adder_8bit_3 (
    .Output2(O[5]), .Output1(O[4]), .Output0(O[3]), .Output4(O[7]), .Output3(O[6]),
    .A2(adder_8bit_2_output3), .B1(O4_1), .A1(adder_8bit_2_output2), .B0(O4_0), .Cin(1'b0),
    .A0(adder_8bit_2_output1), .B7(1'b0), .A7(1'b0), .B6(1'b0), .A6(1'b0), .B5(1'b0), .A5(1'b0), .B4(1'b0),
    .A4(1'b0), .B3(O4_3), .A3(adder_8bit_2_output4), .B2(O4_2));  // open: Cout, Output7, Output6, Output5

  // Other names for the same wires on the sheet: O1_0 = O[0]
endmodule

module ALU (
  input  [7:0] B,
  input  [7:0] A_Accumulator,
  input  A_I_Clear,
  input  CLK,
  input  ACC_I_Enable,
  input  Cin_NBin,
  input  Subtract,
  input  [4:0] ALU_Select,
  input  Enable_ALU,
  output Cout_NBout,
  output N,
  output [7:0] O,
  output Z
);

  wire ADD_0, ADD_1, adder_subtractor_8bit_1_cout, and_1_out, and_2_out, and_3_out, and_4_out, nor_1_out,
       not_1_out, not_2_out, not_3_out, not_4_out, not_5_out, not_6_out, not_7_out, not_8_out, not_9_out,
       not_10_out, not_11_out, not_12_out, not_13_out, not_14_out, not_15_out, not_16_out, not_17_out,
       not_18_out, not_19_out, not_20_out, not_21_out, or_1_out, or_2_out, or_3_out, SHIFT_LEFT,
       shift_left_right_rotate_left_right_1_cout, shift_left_right_rotate_left_right_2_cout, SHIFT_RIGHT,
       SUB_0, SUB_1;
  wire [7:0] adder_subtractor_8bit_1_sum_subtraction, and_8bit_1_o, complement_1_o, multiplier_4bits_1_o,
       nand_8bit_1_o, nor_8bit_1_o, or_8bit_1_o, register_8bit_1_o, shift_left_right_rotate_left_right_1_o,
       shift_left_right_rotate_left_right_2_o, shift_left_right_rotate_left_right_3_o,
       shift_left_right_rotate_left_right_4_o, xnor_8bit_1_o, xor_8bit_1_o;

  Register_8bit register_8bit_1 (
    .O(register_8bit_1_o), .I(A_Accumulator), .Enable(ACC_I_Enable), .CLK(CLK), .CLR(A_I_Clear));
  Adder_Subtractor_8bit adder_subtractor_8bit_1 (
    .Cout(adder_subtractor_8bit_1_cout), .Sum_Subtraction(adder_subtractor_8bit_1_sum_subtraction), .B(B),
    .Sub(Subtract), .A(register_8bit_1_o), .Cin(Cin_NBin));
  AND_8bit and_8bit_1 (.O(and_8bit_1_o), .A(register_8bit_1_o), .B(B));
  OR_8bit or_8bit_1 (.O(or_8bit_1_o), .A(register_8bit_1_o), .B(B));
  NAND_8bit nand_8bit_1 (.O(nand_8bit_1_o), .A(register_8bit_1_o), .B(B));
  NOR_8bit nor_8bit_1 (.O(nor_8bit_1_o), .A(register_8bit_1_o), .B(B));
  XOR_8bit xor_8bit_1 (.O(xor_8bit_1_o), .A(register_8bit_1_o), .B(B));
  XNOR_8bit xnor_8bit_1 (.O(xnor_8bit_1_o), .A(register_8bit_1_o), .B(B));
  Complement complement_1 (.O(complement_1_o), .A(register_8bit_1_o));
  Multiplier_4bits multiplier_4bits_1 (.O(multiplier_4bits_1_o), .A(register_8bit_1_o));
  Shift_Left_Right_Rotate_Left_Right shift_left_right_rotate_left_right_1 (
    .Cout(shift_left_right_rotate_left_right_1_cout), .O(shift_left_right_rotate_left_right_1_o),
    .A(register_8bit_1_o), .S(2'b00));
  Shift_Left_Right_Rotate_Left_Right shift_left_right_rotate_left_right_2 (
    .Cout(shift_left_right_rotate_left_right_2_cout), .O(shift_left_right_rotate_left_right_2_o),
    .A(register_8bit_1_o), .S(2'b01));
  Shift_Left_Right_Rotate_Left_Right shift_left_right_rotate_left_right_3 (
    .O(shift_left_right_rotate_left_right_3_o), .A(register_8bit_1_o), .S(2'b10));  // open: Cout
  Shift_Left_Right_Rotate_Left_Right shift_left_right_rotate_left_right_4 (
    .O(shift_left_right_rotate_left_right_4_o), .A(register_8bit_1_o), .S(2'b11));  // open: Cout
  and and_1 (and_1_out, shift_left_right_rotate_left_right_1_cout, SHIFT_LEFT);
  and and_2 (and_2_out, shift_left_right_rotate_left_right_2_cout, SHIFT_RIGHT);
  or or_1 (or_1_out, and_1_out, and_2_out);
  or or_2 (or_2_out, ADD_0, ADD_1, SUB_0, SUB_1);
  and and_3 (and_3_out, or_2_out, adder_subtractor_8bit_1_cout);
  Multiplexer #(.enable("true"), .select(5), .width(8)) multiplexer_1 (
    .in0(adder_subtractor_8bit_1_sum_subtraction), .in1(adder_subtractor_8bit_1_sum_subtraction),
    .in2(and_8bit_1_o), .in3(and_8bit_1_o), .in4(or_8bit_1_o), .in5(or_8bit_1_o), .in6(nand_8bit_1_o),
    .in7(nor_8bit_1_o), .in8(xor_8bit_1_o), .in9(xor_8bit_1_o), .in10(xnor_8bit_1_o), .in11(complement_1_o),
    .in12(register_8bit_1_o), .in13(adder_subtractor_8bit_1_sum_subtraction),
    .in14(adder_subtractor_8bit_1_sum_subtraction), .in15(multiplier_4bits_1_o),
    .in16(shift_left_right_rotate_left_right_1_o), .in17(shift_left_right_rotate_left_right_2_o),
    .in18(shift_left_right_rotate_left_right_3_o), .in19(shift_left_right_rotate_left_right_4_o),
    .in20(register_8bit_1_o), .in21(register_8bit_1_o), .in22(register_8bit_1_o), .in23(register_8bit_1_o),
    .in24(register_8bit_1_o), .in25(register_8bit_1_o), .in26(register_8bit_1_o), .in27(register_8bit_1_o),
    .in28(register_8bit_1_o), .in29(register_8bit_1_o), .in30(register_8bit_1_o), .in31(register_8bit_1_o),
    .out(O), .sel(ALU_Select), .en(Enable_ALU));
  not not_1 (not_1_out, adder_subtractor_8bit_1_cout);
  not not_2 (not_2_out, ALU_Select[0]);
  not not_3 (not_3_out, ALU_Select[1]);
  not not_4 (not_4_out, ALU_Select[2]);
  not not_5 (not_5_out, ALU_Select[3]);
  not not_6 (not_6_out, ALU_Select[1]);
  not not_7 (not_7_out, ALU_Select[2]);
  not not_8 (not_8_out, ALU_Select[3]);
  not not_9 (not_9_out, ALU_Select[0]);
  not not_10 (not_10_out, ALU_Select[1]);
  not not_11 (not_11_out, ALU_Select[2]);
  not not_12 (not_12_out, ALU_Select[3]);
  not not_13 (not_13_out, ALU_Select[4]);
  not not_14 (not_14_out, ALU_Select[1]);
  not not_15 (not_15_out, ALU_Select[2]);
  not not_16 (not_16_out, ALU_Select[3]);
  not not_17 (not_17_out, ALU_Select[4]);
  not not_18 (not_18_out, ALU_Select[1]);
  not not_19 (not_19_out, ALU_Select[4]);
  not not_20 (not_20_out, ALU_Select[0]);
  not not_21 (not_21_out, ALU_Select[4]);
  or or_3 (or_3_out, and_3_out, or_1_out);
  and and_4 (and_4_out, not_1_out, Subtract);
  nor nor_1 (nor_1_out, O[0], O[1], O[2], O[3], O[4], O[5], O[6], O[7]);
  and and_5 (SHIFT_LEFT, not_2_out, not_3_out, not_4_out, not_5_out, ALU_Select[4]);
  and and_6 (SHIFT_RIGHT, ALU_Select[0], not_6_out, not_7_out, not_8_out, ALU_Select[4]);
  and and_7 (ADD_0, not_9_out, not_10_out, not_11_out, not_12_out, not_13_out);
  and and_8 (ADD_1, ALU_Select[0], not_14_out, not_15_out, not_16_out, not_17_out);
  and and_9 (SUB_0, ALU_Select[0], not_18_out, ALU_Select[2], ALU_Select[3], not_19_out);
  and and_10 (SUB_1, not_20_out, ALU_Select[1], ALU_Select[2], ALU_Select[3], not_21_out);
  and and_11 (Cout_NBout, or_3_out, Enable_ALU);
  and and_12 (N, and_4_out, Enable_ALU);
  and and_13 (Z, nor_1_out, Enable_ALU);

  // Notes on the sheet:
  //   Shift Left
  //   Shift Right
  //   Rotate Left
  //   Rotate Right
endmodule

module Accumulator (
  input  Clear,
  input  CLK,
  input  E_I,
  input  E_BUS_O,
  input  [7:0] ALU_I,
  input  [7:0] BUS_I,
  input  Select_I,
  output [7:0] ALU_O,
  output [7:0] BUS_O
);

  wire [7:0] multiplexer_1_out;

  Multiplexer multiplexer_1 (.in0(ALU_I[0]), .in1(BUS_I[0]), .out(multiplexer_1_out[0]), .sel(Select_I));
  Multiplexer multiplexer_2 (.in0(ALU_I[1]), .in1(BUS_I[1]), .out(multiplexer_1_out[1]), .sel(Select_I));
  Multiplexer multiplexer_3 (.in0(ALU_I[2]), .in1(BUS_I[2]), .out(multiplexer_1_out[2]), .sel(Select_I));
  Multiplexer multiplexer_4 (.in0(ALU_I[3]), .in1(BUS_I[3]), .out(multiplexer_1_out[3]), .sel(Select_I));
  Multiplexer multiplexer_5 (.in0(ALU_I[4]), .in1(BUS_I[4]), .out(multiplexer_1_out[4]), .sel(Select_I));
  Multiplexer multiplexer_6 (.in0(ALU_I[5]), .in1(BUS_I[5]), .out(multiplexer_1_out[5]), .sel(Select_I));
  Multiplexer multiplexer_7 (.in0(ALU_I[6]), .in1(BUS_I[6]), .out(multiplexer_1_out[6]), .sel(Select_I));
  Multiplexer multiplexer_8 (.in0(ALU_I[7]), .in1(BUS_I[7]), .out(multiplexer_1_out[7]), .sel(Select_I));
  Register_8bit register_8bit_1 (.O(ALU_O), .I(multiplexer_1_out), .Enable(E_I), .CLK(CLK), .CLR(Clear));
  Three_State_Output_8bits three_state_output_8bits_1 (.O(BUS_O), .I(ALU_O), .EN(E_BUS_O));
endmodule

module ALU_Accumulator (
  input  [7:0] BUS_Input,
  input  CLK,
  input  A_I_Enable,
  input  A_I_Clear,
  input  Cin_NBin,
  input  Subtract,
  input  ALU_Enable,
  input  [4:0] ALU_Op_Select,
  input  ACC_Select_Input,
  input  ACC_Clear,
  input  ACC_Enable_Input,
  input  ACC_Enable_BUS_Output,
  output [7:0] BUS_Output,
  output Z,
  output N,
  output Cout_NBout
);

  wire [7:0] ACC_Output, ALU_Output;

  ALU alu_1 (
    .O(ALU_Output), .Cout_NBout(Cout_NBout), .N(N), .Z(Z), .A_I_Clear(A_I_Clear), .CLK(CLK),
    .ACC_I_Enable(A_I_Enable), .ALU_Select(ALU_Op_Select), .Enable_ALU(ALU_Enable), .B(BUS_Input),
    .A_Accumulator(ACC_Output), .Cin_NBin(Cin_NBin), .Subtract(Subtract));
  Accumulator accumulator_1 (
    .ALU_O(ACC_Output), .BUS_O(BUS_Output), .ALU_I(ALU_Output), .BUS_I(BUS_Input),
    .Select_I(ACC_Select_Input), .Clear(ACC_Clear), .CLK(CLK), .E_I(ACC_Enable_Input),
    .E_BUS_O(ACC_Enable_BUS_Output));

  // Other names for the same wires on the sheet: ACC_BUS_Output[7:0] = BUS_Output
endmodule

module Status_Register (
  input  Cout_NBout,
  input  Z,
  input  N,
  input  Enable,
  input  CLK,
  input  CLR,
  output Cout_NBout_O,
  output Z_O,
  output N_O
);

  wire multiplexer_1_out, multiplexer_2_out, multiplexer_3_out;

  Multiplexer multiplexer_1 (.in0(Cout_NBout_O), .in1(Cout_NBout), .out(multiplexer_1_out), .sel(Enable));
  Multiplexer multiplexer_2 (.in0(Z_O), .in1(Z), .out(multiplexer_2_out), .sel(Enable));
  Multiplexer multiplexer_3 (.in0(N_O), .in1(N), .out(multiplexer_3_out), .sel(Enable));
  D_Flip_Flop d_ff_1 (.D(multiplexer_1_out), .clk(CLK), .Q(Cout_NBout_O), .reset(CLR));  // open: Qn, preset
  D_Flip_Flop d_ff_2 (.D(multiplexer_2_out), .clk(CLK), .Q(Z_O), .reset(CLR));  // open: Qn, preset
  D_Flip_Flop d_ff_3 (.D(multiplexer_3_out), .clk(CLK), .Q(N_O), .reset(CLR));  // open: Qn, preset

  // Other names for the same wires on the sheet: Q0 = Cout_NBout_O; Q1 = Z_O; Q2 = N_O
endmodule

module Program_Counter (
  input  Count,
  input  Enable_Output,
  input  [7:0] I,
  input  Load,
  input  CLK,
  input  Reset,
  output [7:0] O
);

  wire and_1_out, and_2_out, and_3_out, and_4_out, and_5_out;
  wire [5:0] t_ff_1_q;
  wire [7:0] multiplexer_1_out;

  Multiplexer #(.width(8)) multiplexer_1 (.in0({8{1'b0}}), .in1(I), .out(multiplexer_1_out), .sel(Load));
  and and_1 (and_1_out, t_ff_1_q[0], Count);
  and and_2 (and_2_out, t_ff_1_q[1], and_1_out);
  and and_3 (and_3_out, t_ff_1_q[2], and_2_out);
  and and_4 (and_4_out, t_ff_1_q[3], and_3_out);
  and and_5 (and_5_out, t_ff_1_q[4], and_4_out);
  T_Flip_Flop t_ff_1 (.T(Count), .clk(CLK), .Q(t_ff_1_q[0]), .reset(Reset), .preset(multiplexer_1_out[0]));  // open: Qn
  T_Flip_Flop t_ff_2 (
    .T(and_1_out), .clk(CLK), .Q(t_ff_1_q[1]), .reset(Reset), .preset(multiplexer_1_out[1]));  // open: Qn
  T_Flip_Flop t_ff_3 (
    .T(and_2_out), .clk(CLK), .Q(t_ff_1_q[2]), .reset(Reset), .preset(multiplexer_1_out[2]));  // open: Qn
  T_Flip_Flop t_ff_4 (
    .T(and_3_out), .clk(CLK), .Q(t_ff_1_q[3]), .reset(Reset), .preset(multiplexer_1_out[3]));  // open: Qn
  T_Flip_Flop t_ff_5 (
    .T(and_4_out), .clk(CLK), .Q(t_ff_1_q[4]), .reset(Reset), .preset(multiplexer_1_out[4]));  // open: Qn
  T_Flip_Flop t_ff_6 (
    .T(and_5_out), .clk(CLK), .Q(t_ff_1_q[5]), .reset(Reset), .preset(multiplexer_1_out[5]));  // open: Qn
  Three_State_Output_8bits three_state_output_8bits_1 (.O(O), .I({2'b00, t_ff_1_q}), .EN(Enable_Output));
endmodule

module Instruction_Register (
  input  [7:0] I,
  input  CLR,
  input  CLK,
  input  EN_I,
  input  EN_O,
  input  [7:0] I_Upper,
  output [7:0] O,
  output [7:0] O_Upper
);

  Register_8bit_Three_State_Output register_8bit_three_state_output_1 (
    .O(O), .I(I), .CLR(CLR), .CLK(CLK), .EN_I(EN_I), .EN_O(EN_O));
  Register_8bit_Three_State_Output register_8bit_three_state_output_2 (
    .O(O_Upper), .I(I_Upper), .CLR(CLR), .CLK(CLK), .EN_I(EN_I), .EN_O(EN_O));
endmodule

module MAR (
  input  [7:0] Addrs_I,
  input  CLR,
  input  CLK,
  input  EN,
  output [7:0] Addrs_O
);

  Register_8bit register_8bit_1 (.O(Addrs_O), .I(Addrs_I), .Enable(EN), .CLK(CLK), .CLR(CLR));
endmodule

module MDR (
  input  [7:0] Data_I_BUS,
  input  [7:0] Data_I_RAM,
  input  CLR,
  input  CLK,
  input  Select_I,
  input  Select_O,
  input  EN_I,
  input  EN_O,
  input  [7:0] Data_I_RAM_Upper,
  output [7:0] Data_O_BUS,
  output [7:0] Data_O_RAM,
  output [7:0] Data_O_BUS_Upper
);

  wire [7:0] demultiplexer_1_out0, multiplexer_1_out, register_8bit_1_o, register_8bit_2_o;

  Multiplexer #(.width(8)) multiplexer_1 (.in0(Data_I_BUS), .in1(Data_I_RAM), .out(multiplexer_1_out), .sel(Select_I));
  Demultiplexer #(.width(8)) demultiplexer_1 (
    .out0(demultiplexer_1_out0), .out1(Data_O_RAM), .in(register_8bit_1_o), .sel(Select_O));
  Register_8bit register_8bit_1 (.O(register_8bit_1_o), .I(multiplexer_1_out), .Enable(EN_I), .CLK(CLK), .CLR(CLR));
  Register_8bit register_8bit_2 (.O(register_8bit_2_o), .I(Data_I_RAM_Upper), .Enable(EN_I), .CLK(CLK), .CLR(CLR));
  Three_State_Output_8bits three_state_output_8bits_1 (.O(Data_O_BUS), .I(demultiplexer_1_out0), .EN(EN_O));
  Three_State_Output_8bits three_state_output_8bits_2 (.O(Data_O_BUS_Upper), .I(register_8bit_2_o), .EN(EN_O));
endmodule

module Memory_Cell_8bits (
  input  Column,
  input  Row,
  input  [7:0] I,
  input  NR_W,
  input  CLR,
  input  CLK,
  input  EN_O,
  output [7:0] O
);

  wire Cell_Select, EN_Cell_O, not_1_out;

  not not_1 (not_1_out, NR_W);
  and and_1 (Cell_Select, Column, Row, NR_W);
  and and_2 (EN_Cell_O, Column, Row, not_1_out, EN_O);
  Register_8bit_Three_State_Output register_8bit_three_state_output_1 (
    .O(O), .I(I), .CLR(CLR), .CLK(CLK), .EN_I(Cell_Select), .EN_O(EN_Cell_O));
endmodule

module RAM_256bytes (
  input  [7:0] I,
  input  [7:0] I_Upper,
  input  Enable,
  input  EN_Output,
  input  NR_W,
  input  CLR,
  input  CLK,
  input  [7:0] Addrs,
  output [7:0] O,
  output [7:0] O_Upper
);

  wire Col_0, Col_1, Col_2, Col_3, Col_4, Col_5, Col_6, Col_7, Col_8, Col_9, Col_10, Col_11, Col_12, Col_13,
       Col_14, Col_15, Row_0, Row_1, Row_2, Row_3, Row_4, Row_5, Row_6, Row_7, Row_8, Row_9, Row_10, Row_11,
       Row_12, Row_13, Row_14, Row_15;

  Memory_Cell_8bits memory_cell_8bits_1 (
    .O(O_Upper), .Column(Col_0), .Row(Row_0), .NR_W(NR_W), .EN_O(EN_Output), .I(I_Upper), .CLR(CLR), .CLK(CLK));
  Memory_Cell_8bits memory_cell_8bits_2 (
    .O(O_Upper), .Column(Col_0), .Row(Row_1), .NR_W(NR_W), .EN_O(EN_Output), .I(I_Upper), .CLR(CLR), .CLK(CLK));
  Memory_Cell_8bits memory_cell_8bits_3 (
    .O(O_Upper), .Column(Col_0), .Row(Row_2), .NR_W(NR_W), .EN_O(EN_Output), .I(I_Upper), .CLR(CLR), .CLK(CLK));
  Memory_Cell_8bits memory_cell_8bits_4 (
    .O(O_Upper), .Column(Col_0), .Row(Row_3), .NR_W(NR_W), .EN_O(EN_Output), .I(I_Upper), .CLR(CLR), .CLK(CLK));
  Memory_Cell_8bits memory_cell_8bits_5 (
    .O(O_Upper), .Column(Col_0), .Row(Row_4), .NR_W(NR_W), .EN_O(EN_Output), .I(I_Upper), .CLR(CLR), .CLK(CLK));
  Memory_Cell_8bits memory_cell_8bits_6 (
    .O(O_Upper), .Column(Col_0), .Row(Row_5), .NR_W(NR_W), .EN_O(EN_Output), .I(I_Upper), .CLR(CLR), .CLK(CLK));
  Memory_Cell_8bits memory_cell_8bits_7 (
    .O(O_Upper), .Column(Col_0), .Row(Row_6), .NR_W(NR_W), .EN_O(EN_Output), .I(I_Upper), .CLR(CLR), .CLK(CLK));
  Memory_Cell_8bits memory_cell_8bits_8 (
    .O(O_Upper), .Column(Col_0), .Row(Row_7), .NR_W(NR_W), .EN_O(EN_Output), .I(I_Upper), .CLR(CLR), .CLK(CLK));
  Memory_Cell_8bits memory_cell_8bits_9 (
    .O(O_Upper), .Column(Col_0), .Row(Row_8), .NR_W(NR_W), .EN_O(EN_Output), .I(I_Upper), .CLR(CLR), .CLK(CLK));
  Memory_Cell_8bits memory_cell_8bits_10 (
    .O(O_Upper), .Column(Col_0), .Row(Row_9), .NR_W(NR_W), .EN_O(EN_Output), .I(I_Upper), .CLR(CLR), .CLK(CLK));
  Memory_Cell_8bits memory_cell_8bits_11 (
    .O(O_Upper), .Column(Col_0), .Row(Row_10), .NR_W(NR_W), .EN_O(EN_Output), .I(I_Upper), .CLR(CLR),
    .CLK(CLK));
  Memory_Cell_8bits memory_cell_8bits_12 (
    .O(O_Upper), .Column(Col_0), .Row(Row_11), .NR_W(NR_W), .EN_O(EN_Output), .I(I_Upper), .CLR(CLR),
    .CLK(CLK));
  Memory_Cell_8bits memory_cell_8bits_13 (
    .O(O_Upper), .Column(Col_0), .Row(Row_12), .NR_W(NR_W), .EN_O(EN_Output), .I(I_Upper), .CLR(CLR),
    .CLK(CLK));
  Memory_Cell_8bits memory_cell_8bits_14 (
    .O(O_Upper), .Column(Col_0), .Row(Row_13), .NR_W(NR_W), .EN_O(EN_Output), .I(I_Upper), .CLR(CLR),
    .CLK(CLK));
  Memory_Cell_8bits memory_cell_8bits_15 (
    .O(O_Upper), .Column(Col_0), .Row(Row_14), .NR_W(NR_W), .EN_O(EN_Output), .I(I_Upper), .CLR(CLR),
    .CLK(CLK));
  Memory_Cell_8bits memory_cell_8bits_16 (
    .O(O_Upper), .Column(Col_0), .Row(Row_15), .NR_W(NR_W), .EN_O(EN_Output), .I(I_Upper), .CLR(CLR),
    .CLK(CLK));
  Memory_Cell_8bits memory_cell_8bits_17 (
    .O(O_Upper), .Column(Col_1), .Row(Row_0), .NR_W(NR_W), .EN_O(EN_Output), .I(I_Upper), .CLR(CLR), .CLK(CLK));
  Memory_Cell_8bits memory_cell_8bits_18 (
    .O(O_Upper), .Column(Col_1), .Row(Row_1), .NR_W(NR_W), .EN_O(EN_Output), .I(I_Upper), .CLR(CLR), .CLK(CLK));
  Memory_Cell_8bits memory_cell_8bits_19 (
    .O(O_Upper), .Column(Col_1), .Row(Row_2), .NR_W(NR_W), .EN_O(EN_Output), .I(I_Upper), .CLR(CLR), .CLK(CLK));
  Memory_Cell_8bits memory_cell_8bits_20 (
    .O(O_Upper), .Column(Col_1), .Row(Row_3), .NR_W(NR_W), .EN_O(EN_Output), .I(I_Upper), .CLR(CLR), .CLK(CLK));
  Memory_Cell_8bits memory_cell_8bits_21 (
    .O(O_Upper), .Column(Col_1), .Row(Row_4), .NR_W(NR_W), .EN_O(EN_Output), .I(I_Upper), .CLR(CLR), .CLK(CLK));
  Memory_Cell_8bits memory_cell_8bits_22 (
    .O(O_Upper), .Column(Col_1), .Row(Row_5), .NR_W(NR_W), .EN_O(EN_Output), .I(I_Upper), .CLR(CLR), .CLK(CLK));
  Memory_Cell_8bits memory_cell_8bits_23 (
    .O(O_Upper), .Column(Col_1), .Row(Row_6), .NR_W(NR_W), .EN_O(EN_Output), .I(I_Upper), .CLR(CLR), .CLK(CLK));
  Memory_Cell_8bits memory_cell_8bits_24 (
    .O(O_Upper), .Column(Col_1), .Row(Row_7), .NR_W(NR_W), .EN_O(EN_Output), .I(I_Upper), .CLR(CLR), .CLK(CLK));
  Memory_Cell_8bits memory_cell_8bits_25 (
    .O(O_Upper), .Column(Col_1), .Row(Row_8), .NR_W(NR_W), .EN_O(EN_Output), .I(I_Upper), .CLR(CLR), .CLK(CLK));
  Memory_Cell_8bits memory_cell_8bits_26 (
    .O(O_Upper), .Column(Col_1), .Row(Row_9), .NR_W(NR_W), .EN_O(EN_Output), .I(I_Upper), .CLR(CLR), .CLK(CLK));
  Memory_Cell_8bits memory_cell_8bits_27 (
    .O(O_Upper), .Column(Col_1), .Row(Row_10), .NR_W(NR_W), .EN_O(EN_Output), .I(I_Upper), .CLR(CLR),
    .CLK(CLK));
  Memory_Cell_8bits memory_cell_8bits_28 (
    .O(O_Upper), .Column(Col_1), .Row(Row_11), .NR_W(NR_W), .EN_O(EN_Output), .I(I_Upper), .CLR(CLR),
    .CLK(CLK));
  Memory_Cell_8bits memory_cell_8bits_29 (
    .O(O_Upper), .Column(Col_1), .Row(Row_12), .NR_W(NR_W), .EN_O(EN_Output), .I(I_Upper), .CLR(CLR),
    .CLK(CLK));
  Memory_Cell_8bits memory_cell_8bits_30 (
    .O(O_Upper), .Column(Col_1), .Row(Row_13), .NR_W(NR_W), .EN_O(EN_Output), .I(I_Upper), .CLR(CLR),
    .CLK(CLK));
  Memory_Cell_8bits memory_cell_8bits_31 (
    .O(O_Upper), .Column(Col_1), .Row(Row_14), .NR_W(NR_W), .EN_O(EN_Output), .I(I_Upper), .CLR(CLR),
    .CLK(CLK));
  Memory_Cell_8bits memory_cell_8bits_32 (
    .O(O_Upper), .Column(Col_1), .Row(Row_15), .NR_W(NR_W), .EN_O(EN_Output), .I(I_Upper), .CLR(CLR),
    .CLK(CLK));
  Memory_Cell_8bits memory_cell_8bits_33 (
    .O(O_Upper), .Column(Col_2), .Row(Row_0), .NR_W(NR_W), .EN_O(EN_Output), .I(I_Upper), .CLR(CLR), .CLK(CLK));
  Memory_Cell_8bits memory_cell_8bits_34 (
    .O(O_Upper), .Column(Col_2), .Row(Row_1), .NR_W(NR_W), .EN_O(EN_Output), .I(I_Upper), .CLR(CLR), .CLK(CLK));
  Memory_Cell_8bits memory_cell_8bits_35 (
    .O(O_Upper), .Column(Col_2), .Row(Row_2), .NR_W(NR_W), .EN_O(EN_Output), .I(I_Upper), .CLR(CLR), .CLK(CLK));
  Memory_Cell_8bits memory_cell_8bits_36 (
    .O(O_Upper), .Column(Col_2), .Row(Row_3), .NR_W(NR_W), .EN_O(EN_Output), .I(I_Upper), .CLR(CLR), .CLK(CLK));
  Memory_Cell_8bits memory_cell_8bits_37 (
    .O(O_Upper), .Column(Col_2), .Row(Row_4), .NR_W(NR_W), .EN_O(EN_Output), .I(I_Upper), .CLR(CLR), .CLK(CLK));
  Memory_Cell_8bits memory_cell_8bits_38 (
    .O(O_Upper), .Column(Col_2), .Row(Row_5), .NR_W(NR_W), .EN_O(EN_Output), .I(I_Upper), .CLR(CLR), .CLK(CLK));
  Memory_Cell_8bits memory_cell_8bits_39 (
    .O(O_Upper), .Column(Col_2), .Row(Row_6), .NR_W(NR_W), .EN_O(EN_Output), .I(I_Upper), .CLR(CLR), .CLK(CLK));
  Memory_Cell_8bits memory_cell_8bits_40 (
    .O(O_Upper), .Column(Col_2), .Row(Row_7), .NR_W(NR_W), .EN_O(EN_Output), .I(I_Upper), .CLR(CLR), .CLK(CLK));
  Memory_Cell_8bits memory_cell_8bits_41 (
    .O(O_Upper), .Column(Col_2), .Row(Row_8), .NR_W(NR_W), .EN_O(EN_Output), .I(I_Upper), .CLR(CLR), .CLK(CLK));
  Memory_Cell_8bits memory_cell_8bits_42 (
    .O(O_Upper), .Column(Col_2), .Row(Row_9), .NR_W(NR_W), .EN_O(EN_Output), .I(I_Upper), .CLR(CLR), .CLK(CLK));
  Memory_Cell_8bits memory_cell_8bits_43 (
    .O(O_Upper), .Column(Col_2), .Row(Row_10), .NR_W(NR_W), .EN_O(EN_Output), .I(I_Upper), .CLR(CLR),
    .CLK(CLK));
  Memory_Cell_8bits memory_cell_8bits_44 (
    .O(O_Upper), .Column(Col_2), .Row(Row_11), .NR_W(NR_W), .EN_O(EN_Output), .I(I_Upper), .CLR(CLR),
    .CLK(CLK));
  Memory_Cell_8bits memory_cell_8bits_45 (
    .O(O_Upper), .Column(Col_2), .Row(Row_12), .NR_W(NR_W), .EN_O(EN_Output), .I(I_Upper), .CLR(CLR),
    .CLK(CLK));
  Memory_Cell_8bits memory_cell_8bits_46 (
    .O(O_Upper), .Column(Col_2), .Row(Row_13), .NR_W(NR_W), .EN_O(EN_Output), .I(I_Upper), .CLR(CLR),
    .CLK(CLK));
  Memory_Cell_8bits memory_cell_8bits_47 (
    .O(O_Upper), .Column(Col_2), .Row(Row_14), .NR_W(NR_W), .EN_O(EN_Output), .I(I_Upper), .CLR(CLR),
    .CLK(CLK));
  Memory_Cell_8bits memory_cell_8bits_48 (
    .O(O_Upper), .Column(Col_2), .Row(Row_15), .NR_W(NR_W), .EN_O(EN_Output), .I(I_Upper), .CLR(CLR),
    .CLK(CLK));
  Memory_Cell_8bits memory_cell_8bits_49 (
    .O(O_Upper), .Column(Col_3), .Row(Row_0), .NR_W(NR_W), .EN_O(EN_Output), .I(I_Upper), .CLR(CLR), .CLK(CLK));
  Memory_Cell_8bits memory_cell_8bits_50 (
    .O(O_Upper), .Column(Col_3), .Row(Row_1), .NR_W(NR_W), .EN_O(EN_Output), .I(I_Upper), .CLR(CLR), .CLK(CLK));
  Memory_Cell_8bits memory_cell_8bits_51 (
    .O(O_Upper), .Column(Col_3), .Row(Row_2), .NR_W(NR_W), .EN_O(EN_Output), .I(I_Upper), .CLR(CLR), .CLK(CLK));
  Memory_Cell_8bits memory_cell_8bits_52 (
    .O(O_Upper), .Column(Col_3), .Row(Row_3), .NR_W(NR_W), .EN_O(EN_Output), .I(I_Upper), .CLR(CLR), .CLK(CLK));
  Memory_Cell_8bits memory_cell_8bits_53 (
    .O(O_Upper), .Column(Col_3), .Row(Row_4), .NR_W(NR_W), .EN_O(EN_Output), .I(I_Upper), .CLR(CLR), .CLK(CLK));
  Memory_Cell_8bits memory_cell_8bits_54 (
    .O(O_Upper), .Column(Col_3), .Row(Row_5), .NR_W(NR_W), .EN_O(EN_Output), .I(I_Upper), .CLR(CLR), .CLK(CLK));
  Memory_Cell_8bits memory_cell_8bits_55 (
    .O(O_Upper), .Column(Col_3), .Row(Row_6), .NR_W(NR_W), .EN_O(EN_Output), .I(I_Upper), .CLR(CLR), .CLK(CLK));
  Memory_Cell_8bits memory_cell_8bits_56 (
    .O(O_Upper), .Column(Col_3), .Row(Row_7), .NR_W(NR_W), .EN_O(EN_Output), .I(I_Upper), .CLR(CLR), .CLK(CLK));
  Memory_Cell_8bits memory_cell_8bits_57 (
    .O(O_Upper), .Column(Col_3), .Row(Row_8), .NR_W(NR_W), .EN_O(EN_Output), .I(I_Upper), .CLR(CLR), .CLK(CLK));
  Memory_Cell_8bits memory_cell_8bits_58 (
    .O(O_Upper), .Column(Col_3), .Row(Row_9), .NR_W(NR_W), .EN_O(EN_Output), .I(I_Upper), .CLR(CLR), .CLK(CLK));
  Memory_Cell_8bits memory_cell_8bits_59 (
    .O(O_Upper), .Column(Col_3), .Row(Row_10), .NR_W(NR_W), .EN_O(EN_Output), .I(I_Upper), .CLR(CLR),
    .CLK(CLK));
  Memory_Cell_8bits memory_cell_8bits_60 (
    .O(O_Upper), .Column(Col_3), .Row(Row_11), .NR_W(NR_W), .EN_O(EN_Output), .I(I_Upper), .CLR(CLR),
    .CLK(CLK));
  Memory_Cell_8bits memory_cell_8bits_61 (
    .O(O_Upper), .Column(Col_3), .Row(Row_12), .NR_W(NR_W), .EN_O(EN_Output), .I(I_Upper), .CLR(CLR),
    .CLK(CLK));
  Memory_Cell_8bits memory_cell_8bits_62 (
    .O(O_Upper), .Column(Col_3), .Row(Row_13), .NR_W(NR_W), .EN_O(EN_Output), .I(I_Upper), .CLR(CLR),
    .CLK(CLK));
  Memory_Cell_8bits memory_cell_8bits_63 (
    .O(O_Upper), .Column(Col_3), .Row(Row_14), .NR_W(NR_W), .EN_O(EN_Output), .I(I_Upper), .CLR(CLR),
    .CLK(CLK));
  Memory_Cell_8bits memory_cell_8bits_64 (
    .O(O_Upper), .Column(Col_3), .Row(Row_15), .NR_W(NR_W), .EN_O(EN_Output), .I(I_Upper), .CLR(CLR),
    .CLK(CLK));
  Memory_Cell_8bits memory_cell_8bits_65 (
    .O(O), .Column(Col_0), .Row(Row_0), .NR_W(NR_W), .EN_O(EN_Output), .I(I), .CLR(CLR), .CLK(CLK));
  Memory_Cell_8bits memory_cell_8bits_66 (
    .O(O), .Column(Col_0), .Row(Row_1), .NR_W(NR_W), .EN_O(EN_Output), .I(I), .CLR(CLR), .CLK(CLK));
  Memory_Cell_8bits memory_cell_8bits_67 (
    .O(O), .Column(Col_0), .Row(Row_2), .NR_W(NR_W), .EN_O(EN_Output), .I(I), .CLR(CLR), .CLK(CLK));
  Memory_Cell_8bits memory_cell_8bits_68 (
    .O(O), .Column(Col_0), .Row(Row_3), .NR_W(NR_W), .EN_O(EN_Output), .I(I), .CLR(CLR), .CLK(CLK));
  Memory_Cell_8bits memory_cell_8bits_69 (
    .O(O), .Column(Col_0), .Row(Row_4), .NR_W(NR_W), .EN_O(EN_Output), .I(I), .CLR(CLR), .CLK(CLK));
  Memory_Cell_8bits memory_cell_8bits_70 (
    .O(O), .Column(Col_0), .Row(Row_5), .NR_W(NR_W), .EN_O(EN_Output), .I(I), .CLR(CLR), .CLK(CLK));
  Memory_Cell_8bits memory_cell_8bits_71 (
    .O(O), .Column(Col_0), .Row(Row_6), .NR_W(NR_W), .EN_O(EN_Output), .I(I), .CLR(CLR), .CLK(CLK));
  Memory_Cell_8bits memory_cell_8bits_72 (
    .O(O), .Column(Col_0), .Row(Row_7), .NR_W(NR_W), .EN_O(EN_Output), .I(I), .CLR(CLR), .CLK(CLK));
  Memory_Cell_8bits memory_cell_8bits_73 (
    .O(O), .Column(Col_0), .Row(Row_8), .NR_W(NR_W), .EN_O(EN_Output), .I(I), .CLR(CLR), .CLK(CLK));
  Memory_Cell_8bits memory_cell_8bits_74 (
    .O(O), .Column(Col_0), .Row(Row_9), .NR_W(NR_W), .EN_O(EN_Output), .I(I), .CLR(CLR), .CLK(CLK));
  Memory_Cell_8bits memory_cell_8bits_75 (
    .O(O), .Column(Col_0), .Row(Row_10), .NR_W(NR_W), .EN_O(EN_Output), .I(I), .CLR(CLR), .CLK(CLK));
  Memory_Cell_8bits memory_cell_8bits_76 (
    .O(O), .Column(Col_0), .Row(Row_11), .NR_W(NR_W), .EN_O(EN_Output), .I(I), .CLR(CLR), .CLK(CLK));
  Memory_Cell_8bits memory_cell_8bits_77 (
    .O(O), .Column(Col_0), .Row(Row_12), .NR_W(NR_W), .EN_O(EN_Output), .I(I), .CLR(CLR), .CLK(CLK));
  Memory_Cell_8bits memory_cell_8bits_78 (
    .O(O), .Column(Col_0), .Row(Row_13), .NR_W(NR_W), .EN_O(EN_Output), .I(I), .CLR(CLR), .CLK(CLK));
  Memory_Cell_8bits memory_cell_8bits_79 (
    .O(O), .Column(Col_0), .Row(Row_14), .NR_W(NR_W), .EN_O(EN_Output), .I(I), .CLR(CLR), .CLK(CLK));
  Memory_Cell_8bits memory_cell_8bits_80 (
    .O(O), .Column(Col_0), .Row(Row_15), .NR_W(NR_W), .EN_O(EN_Output), .I(I), .CLR(CLR), .CLK(CLK));
  Memory_Cell_8bits memory_cell_8bits_81 (
    .O(O), .Column(Col_1), .Row(Row_0), .NR_W(NR_W), .EN_O(EN_Output), .I(I), .CLR(CLR), .CLK(CLK));
  Memory_Cell_8bits memory_cell_8bits_82 (
    .O(O), .Column(Col_1), .Row(Row_1), .NR_W(NR_W), .EN_O(EN_Output), .I(I), .CLR(CLR), .CLK(CLK));
  Memory_Cell_8bits memory_cell_8bits_83 (
    .O(O), .Column(Col_1), .Row(Row_2), .NR_W(NR_W), .EN_O(EN_Output), .I(I), .CLR(CLR), .CLK(CLK));
  Memory_Cell_8bits memory_cell_8bits_84 (
    .O(O), .Column(Col_1), .Row(Row_3), .NR_W(NR_W), .EN_O(EN_Output), .I(I), .CLR(CLR), .CLK(CLK));
  Memory_Cell_8bits memory_cell_8bits_85 (
    .O(O), .Column(Col_1), .Row(Row_4), .NR_W(NR_W), .EN_O(EN_Output), .I(I), .CLR(CLR), .CLK(CLK));
  Memory_Cell_8bits memory_cell_8bits_86 (
    .O(O), .Column(Col_1), .Row(Row_5), .NR_W(NR_W), .EN_O(EN_Output), .I(I), .CLR(CLR), .CLK(CLK));
  Memory_Cell_8bits memory_cell_8bits_87 (
    .O(O), .Column(Col_1), .Row(Row_6), .NR_W(NR_W), .EN_O(EN_Output), .I(I), .CLR(CLR), .CLK(CLK));
  Memory_Cell_8bits memory_cell_8bits_88 (
    .O(O), .Column(Col_1), .Row(Row_7), .NR_W(NR_W), .EN_O(EN_Output), .I(I), .CLR(CLR), .CLK(CLK));
  Memory_Cell_8bits memory_cell_8bits_89 (
    .O(O), .Column(Col_1), .Row(Row_8), .NR_W(NR_W), .EN_O(EN_Output), .I(I), .CLR(CLR), .CLK(CLK));
  Memory_Cell_8bits memory_cell_8bits_90 (
    .O(O), .Column(Col_1), .Row(Row_9), .NR_W(NR_W), .EN_O(EN_Output), .I(I), .CLR(CLR), .CLK(CLK));
  Memory_Cell_8bits memory_cell_8bits_91 (
    .O(O), .Column(Col_1), .Row(Row_10), .NR_W(NR_W), .EN_O(EN_Output), .I(I), .CLR(CLR), .CLK(CLK));
  Memory_Cell_8bits memory_cell_8bits_92 (
    .O(O), .Column(Col_1), .Row(Row_11), .NR_W(NR_W), .EN_O(EN_Output), .I(I), .CLR(CLR), .CLK(CLK));
  Memory_Cell_8bits memory_cell_8bits_93 (
    .O(O), .Column(Col_1), .Row(Row_12), .NR_W(NR_W), .EN_O(EN_Output), .I(I), .CLR(CLR), .CLK(CLK));
  Memory_Cell_8bits memory_cell_8bits_94 (
    .O(O), .Column(Col_1), .Row(Row_13), .NR_W(NR_W), .EN_O(EN_Output), .I(I), .CLR(CLR), .CLK(CLK));
  Memory_Cell_8bits memory_cell_8bits_95 (
    .O(O), .Column(Col_1), .Row(Row_14), .NR_W(NR_W), .EN_O(EN_Output), .I(I), .CLR(CLR), .CLK(CLK));
  Memory_Cell_8bits memory_cell_8bits_96 (
    .O(O), .Column(Col_1), .Row(Row_15), .NR_W(NR_W), .EN_O(EN_Output), .I(I), .CLR(CLR), .CLK(CLK));
  Memory_Cell_8bits memory_cell_8bits_97 (
    .O(O), .Column(Col_2), .Row(Row_8), .NR_W(NR_W), .EN_O(EN_Output), .I(I), .CLR(CLR), .CLK(CLK));
  Memory_Cell_8bits memory_cell_8bits_98 (
    .O(O), .Column(Col_2), .Row(Row_9), .NR_W(NR_W), .EN_O(EN_Output), .I(I), .CLR(CLR), .CLK(CLK));
  Memory_Cell_8bits memory_cell_8bits_99 (
    .O(O), .Column(Col_2), .Row(Row_10), .NR_W(NR_W), .EN_O(EN_Output), .I(I), .CLR(CLR), .CLK(CLK));
  Memory_Cell_8bits memory_cell_8bits_100 (
    .O(O), .Column(Col_2), .Row(Row_11), .NR_W(NR_W), .EN_O(EN_Output), .I(I), .CLR(CLR), .CLK(CLK));
  Memory_Cell_8bits memory_cell_8bits_101 (
    .O(O), .Column(Col_2), .Row(Row_12), .NR_W(NR_W), .EN_O(EN_Output), .I(I), .CLR(CLR), .CLK(CLK));
  Memory_Cell_8bits memory_cell_8bits_102 (
    .O(O), .Column(Col_2), .Row(Row_13), .NR_W(NR_W), .EN_O(EN_Output), .I(I), .CLR(CLR), .CLK(CLK));
  Memory_Cell_8bits memory_cell_8bits_103 (
    .O(O), .Column(Col_2), .Row(Row_14), .NR_W(NR_W), .EN_O(EN_Output), .I(I), .CLR(CLR), .CLK(CLK));
  Memory_Cell_8bits memory_cell_8bits_104 (
    .O(O), .Column(Col_2), .Row(Row_15), .NR_W(NR_W), .EN_O(EN_Output), .I(I), .CLR(CLR), .CLK(CLK));
  Memory_Cell_8bits memory_cell_8bits_105 (
    .O(O), .Column(Col_2), .Row(Row_0), .NR_W(NR_W), .EN_O(EN_Output), .I(I), .CLR(CLR), .CLK(CLK));
  Memory_Cell_8bits memory_cell_8bits_106 (
    .O(O), .Column(Col_2), .Row(Row_1), .NR_W(NR_W), .EN_O(EN_Output), .I(I), .CLR(CLR), .CLK(CLK));
  Memory_Cell_8bits memory_cell_8bits_107 (
    .O(O), .Column(Col_2), .Row(Row_2), .NR_W(NR_W), .EN_O(EN_Output), .I(I), .CLR(CLR), .CLK(CLK));
  Memory_Cell_8bits memory_cell_8bits_108 (
    .O(O), .Column(Col_2), .Row(Row_3), .NR_W(NR_W), .EN_O(EN_Output), .I(I), .CLR(CLR), .CLK(CLK));
  Memory_Cell_8bits memory_cell_8bits_109 (
    .O(O), .Column(Col_2), .Row(Row_4), .NR_W(NR_W), .EN_O(EN_Output), .I(I), .CLR(CLR), .CLK(CLK));
  Memory_Cell_8bits memory_cell_8bits_110 (
    .O(O), .Column(Col_2), .Row(Row_5), .NR_W(NR_W), .EN_O(EN_Output), .I(I), .CLR(CLR), .CLK(CLK));
  Memory_Cell_8bits memory_cell_8bits_111 (
    .O(O), .Column(Col_2), .Row(Row_6), .NR_W(NR_W), .EN_O(EN_Output), .I(I), .CLR(CLR), .CLK(CLK));
  Memory_Cell_8bits memory_cell_8bits_112 (
    .O(O), .Column(Col_2), .Row(Row_7), .NR_W(NR_W), .EN_O(EN_Output), .I(I), .CLR(CLR), .CLK(CLK));
  Memory_Cell_8bits memory_cell_8bits_113 (
    .O(O), .Column(Col_3), .Row(Row_0), .NR_W(NR_W), .EN_O(EN_Output), .I(I), .CLR(CLR), .CLK(CLK));
  Memory_Cell_8bits memory_cell_8bits_114 (
    .O(O), .Column(Col_3), .Row(Row_1), .NR_W(NR_W), .EN_O(EN_Output), .I(I), .CLR(CLR), .CLK(CLK));
  Memory_Cell_8bits memory_cell_8bits_115 (
    .O(O), .Column(Col_3), .Row(Row_2), .NR_W(NR_W), .EN_O(EN_Output), .I(I), .CLR(CLR), .CLK(CLK));
  Memory_Cell_8bits memory_cell_8bits_116 (
    .O(O), .Column(Col_3), .Row(Row_3), .NR_W(NR_W), .EN_O(EN_Output), .I(I), .CLR(CLR), .CLK(CLK));
  Memory_Cell_8bits memory_cell_8bits_117 (
    .O(O), .Column(Col_3), .Row(Row_4), .NR_W(NR_W), .EN_O(EN_Output), .I(I), .CLR(CLR), .CLK(CLK));
  Memory_Cell_8bits memory_cell_8bits_118 (
    .O(O), .Column(Col_3), .Row(Row_5), .NR_W(NR_W), .EN_O(EN_Output), .I(I), .CLR(CLR), .CLK(CLK));
  Memory_Cell_8bits memory_cell_8bits_119 (
    .O(O), .Column(Col_3), .Row(Row_6), .NR_W(NR_W), .EN_O(EN_Output), .I(I), .CLR(CLR), .CLK(CLK));
  Memory_Cell_8bits memory_cell_8bits_120 (
    .O(O), .Column(Col_3), .Row(Row_7), .NR_W(NR_W), .EN_O(EN_Output), .I(I), .CLR(CLR), .CLK(CLK));
  Memory_Cell_8bits memory_cell_8bits_121 (
    .O(O), .Column(Col_3), .Row(Row_8), .NR_W(NR_W), .EN_O(EN_Output), .I(I), .CLR(CLR), .CLK(CLK));
  Memory_Cell_8bits memory_cell_8bits_122 (
    .O(O), .Column(Col_3), .Row(Row_9), .NR_W(NR_W), .EN_O(EN_Output), .I(I), .CLR(CLR), .CLK(CLK));
  Memory_Cell_8bits memory_cell_8bits_123 (
    .O(O), .Column(Col_3), .Row(Row_10), .NR_W(NR_W), .EN_O(EN_Output), .I(I), .CLR(CLR), .CLK(CLK));
  Memory_Cell_8bits memory_cell_8bits_124 (
    .O(O), .Column(Col_3), .Row(Row_11), .NR_W(NR_W), .EN_O(EN_Output), .I(I), .CLR(CLR), .CLK(CLK));
  Memory_Cell_8bits memory_cell_8bits_125 (
    .O(O), .Column(Col_3), .Row(Row_12), .NR_W(NR_W), .EN_O(EN_Output), .I(I), .CLR(CLR), .CLK(CLK));
  Memory_Cell_8bits memory_cell_8bits_126 (
    .O(O), .Column(Col_3), .Row(Row_13), .NR_W(NR_W), .EN_O(EN_Output), .I(I), .CLR(CLR), .CLK(CLK));
  Memory_Cell_8bits memory_cell_8bits_127 (
    .O(O), .Column(Col_3), .Row(Row_14), .NR_W(NR_W), .EN_O(EN_Output), .I(I), .CLR(CLR), .CLK(CLK));
  Memory_Cell_8bits memory_cell_8bits_128 (
    .O(O), .Column(Col_3), .Row(Row_15), .NR_W(NR_W), .EN_O(EN_Output), .I(I), .CLR(CLR), .CLK(CLK));
  Memory_Cell_8bits memory_cell_8bits_129 (
    .O(O), .Column(Col_4), .Row(Row_0), .NR_W(NR_W), .EN_O(EN_Output), .I(I), .CLR(CLR), .CLK(CLK));
  Memory_Cell_8bits memory_cell_8bits_130 (
    .O(O), .Column(Col_4), .Row(Row_1), .NR_W(NR_W), .EN_O(EN_Output), .I(I), .CLR(CLR), .CLK(CLK));
  Memory_Cell_8bits memory_cell_8bits_131 (
    .O(O), .Column(Col_4), .Row(Row_2), .NR_W(NR_W), .EN_O(EN_Output), .I(I), .CLR(CLR), .CLK(CLK));
  Memory_Cell_8bits memory_cell_8bits_132 (
    .O(O), .Column(Col_4), .Row(Row_3), .NR_W(NR_W), .EN_O(EN_Output), .I(I), .CLR(CLR), .CLK(CLK));
  Memory_Cell_8bits memory_cell_8bits_133 (
    .O(O), .Column(Col_4), .Row(Row_4), .NR_W(NR_W), .EN_O(EN_Output), .I(I), .CLR(CLR), .CLK(CLK));
  Memory_Cell_8bits memory_cell_8bits_134 (
    .O(O), .Column(Col_4), .Row(Row_5), .NR_W(NR_W), .EN_O(EN_Output), .I(I), .CLR(CLR), .CLK(CLK));
  Memory_Cell_8bits memory_cell_8bits_135 (
    .O(O), .Column(Col_4), .Row(Row_6), .NR_W(NR_W), .EN_O(EN_Output), .I(I), .CLR(CLR), .CLK(CLK));
  Memory_Cell_8bits memory_cell_8bits_136 (
    .O(O), .Column(Col_4), .Row(Row_7), .NR_W(NR_W), .EN_O(EN_Output), .I(I), .CLR(CLR), .CLK(CLK));
  Memory_Cell_8bits memory_cell_8bits_137 (
    .O(O), .Column(Col_4), .Row(Row_8), .NR_W(NR_W), .EN_O(EN_Output), .I(I), .CLR(CLR), .CLK(CLK));
  Memory_Cell_8bits memory_cell_8bits_138 (
    .O(O), .Column(Col_4), .Row(Row_9), .NR_W(NR_W), .EN_O(EN_Output), .I(I), .CLR(CLR), .CLK(CLK));
  Memory_Cell_8bits memory_cell_8bits_139 (
    .O(O), .Column(Col_4), .Row(Row_10), .NR_W(NR_W), .EN_O(EN_Output), .I(I), .CLR(CLR), .CLK(CLK));
  Memory_Cell_8bits memory_cell_8bits_140 (
    .O(O), .Column(Col_4), .Row(Row_11), .NR_W(NR_W), .EN_O(EN_Output), .I(I), .CLR(CLR), .CLK(CLK));
  Memory_Cell_8bits memory_cell_8bits_141 (
    .O(O), .Column(Col_4), .Row(Row_12), .NR_W(NR_W), .EN_O(EN_Output), .I(I), .CLR(CLR), .CLK(CLK));
  Memory_Cell_8bits memory_cell_8bits_142 (
    .O(O), .Column(Col_4), .Row(Row_13), .NR_W(NR_W), .EN_O(EN_Output), .I(I), .CLR(CLR), .CLK(CLK));
  Memory_Cell_8bits memory_cell_8bits_143 (
    .O(O), .Column(Col_4), .Row(Row_14), .NR_W(NR_W), .EN_O(EN_Output), .I(I), .CLR(CLR), .CLK(CLK));
  Memory_Cell_8bits memory_cell_8bits_144 (
    .O(O), .Column(Col_4), .Row(Row_15), .NR_W(NR_W), .EN_O(EN_Output), .I(I), .CLR(CLR), .CLK(CLK));
  Memory_Cell_8bits memory_cell_8bits_145 (
    .O(O), .Column(Col_5), .Row(Row_0), .NR_W(NR_W), .EN_O(EN_Output), .I(I), .CLR(CLR), .CLK(CLK));
  Memory_Cell_8bits memory_cell_8bits_146 (
    .O(O), .Column(Col_5), .Row(Row_1), .NR_W(NR_W), .EN_O(EN_Output), .I(I), .CLR(CLR), .CLK(CLK));
  Memory_Cell_8bits memory_cell_8bits_147 (
    .O(O), .Column(Col_5), .Row(Row_2), .NR_W(NR_W), .EN_O(EN_Output), .I(I), .CLR(CLR), .CLK(CLK));
  Memory_Cell_8bits memory_cell_8bits_148 (
    .O(O), .Column(Col_5), .Row(Row_3), .NR_W(NR_W), .EN_O(EN_Output), .I(I), .CLR(CLR), .CLK(CLK));
  Memory_Cell_8bits memory_cell_8bits_149 (
    .O(O), .Column(Col_5), .Row(Row_4), .NR_W(NR_W), .EN_O(EN_Output), .I(I), .CLR(CLR), .CLK(CLK));
  Memory_Cell_8bits memory_cell_8bits_150 (
    .O(O), .Column(Col_5), .Row(Row_5), .NR_W(NR_W), .EN_O(EN_Output), .I(I), .CLR(CLR), .CLK(CLK));
  Memory_Cell_8bits memory_cell_8bits_151 (
    .O(O), .Column(Col_5), .Row(Row_6), .NR_W(NR_W), .EN_O(EN_Output), .I(I), .CLR(CLR), .CLK(CLK));
  Memory_Cell_8bits memory_cell_8bits_152 (
    .O(O), .Column(Col_5), .Row(Row_7), .NR_W(NR_W), .EN_O(EN_Output), .I(I), .CLR(CLR), .CLK(CLK));
  Memory_Cell_8bits memory_cell_8bits_153 (
    .O(O), .Column(Col_5), .Row(Row_8), .NR_W(NR_W), .EN_O(EN_Output), .I(I), .CLR(CLR), .CLK(CLK));
  Memory_Cell_8bits memory_cell_8bits_154 (
    .O(O), .Column(Col_5), .Row(Row_9), .NR_W(NR_W), .EN_O(EN_Output), .I(I), .CLR(CLR), .CLK(CLK));
  Memory_Cell_8bits memory_cell_8bits_155 (
    .O(O), .Column(Col_5), .Row(Row_10), .NR_W(NR_W), .EN_O(EN_Output), .I(I), .CLR(CLR), .CLK(CLK));
  Memory_Cell_8bits memory_cell_8bits_156 (
    .O(O), .Column(Col_5), .Row(Row_11), .NR_W(NR_W), .EN_O(EN_Output), .I(I), .CLR(CLR), .CLK(CLK));
  Memory_Cell_8bits memory_cell_8bits_157 (
    .O(O), .Column(Col_5), .Row(Row_12), .NR_W(NR_W), .EN_O(EN_Output), .I(I), .CLR(CLR), .CLK(CLK));
  Memory_Cell_8bits memory_cell_8bits_158 (
    .O(O), .Column(Col_5), .Row(Row_13), .NR_W(NR_W), .EN_O(EN_Output), .I(I), .CLR(CLR), .CLK(CLK));
  Memory_Cell_8bits memory_cell_8bits_159 (
    .O(O), .Column(Col_5), .Row(Row_14), .NR_W(NR_W), .EN_O(EN_Output), .I(I), .CLR(CLR), .CLK(CLK));
  Memory_Cell_8bits memory_cell_8bits_160 (
    .O(O), .Column(Col_5), .Row(Row_15), .NR_W(NR_W), .EN_O(EN_Output), .I(I), .CLR(CLR), .CLK(CLK));
  Memory_Cell_8bits memory_cell_8bits_161 (
    .O(O), .Column(Col_6), .Row(Row_0), .NR_W(NR_W), .EN_O(EN_Output), .I(I), .CLR(CLR), .CLK(CLK));
  Memory_Cell_8bits memory_cell_8bits_162 (
    .O(O), .Column(Col_6), .Row(Row_1), .NR_W(NR_W), .EN_O(EN_Output), .I(I), .CLR(CLR), .CLK(CLK));
  Memory_Cell_8bits memory_cell_8bits_163 (
    .O(O), .Column(Col_6), .Row(Row_2), .NR_W(NR_W), .EN_O(EN_Output), .I(I), .CLR(CLR), .CLK(CLK));
  Memory_Cell_8bits memory_cell_8bits_164 (
    .O(O), .Column(Col_6), .Row(Row_3), .NR_W(NR_W), .EN_O(EN_Output), .I(I), .CLR(CLR), .CLK(CLK));
  Memory_Cell_8bits memory_cell_8bits_165 (
    .O(O), .Column(Col_6), .Row(Row_4), .NR_W(NR_W), .EN_O(EN_Output), .I(I), .CLR(CLR), .CLK(CLK));
  Memory_Cell_8bits memory_cell_8bits_166 (
    .O(O), .Column(Col_6), .Row(Row_5), .NR_W(NR_W), .EN_O(EN_Output), .I(I), .CLR(CLR), .CLK(CLK));
  Memory_Cell_8bits memory_cell_8bits_167 (
    .O(O), .Column(Col_6), .Row(Row_6), .NR_W(NR_W), .EN_O(EN_Output), .I(I), .CLR(CLR), .CLK(CLK));
  Memory_Cell_8bits memory_cell_8bits_168 (
    .O(O), .Column(Col_6), .Row(Row_7), .NR_W(NR_W), .EN_O(EN_Output), .I(I), .CLR(CLR), .CLK(CLK));
  Memory_Cell_8bits memory_cell_8bits_169 (
    .O(O), .Column(Col_6), .Row(Row_8), .NR_W(NR_W), .EN_O(EN_Output), .I(I), .CLR(CLR), .CLK(CLK));
  Memory_Cell_8bits memory_cell_8bits_170 (
    .O(O), .Column(Col_6), .Row(Row_9), .NR_W(NR_W), .EN_O(EN_Output), .I(I), .CLR(CLR), .CLK(CLK));
  Memory_Cell_8bits memory_cell_8bits_171 (
    .O(O), .Column(Col_6), .Row(Row_10), .NR_W(NR_W), .EN_O(EN_Output), .I(I), .CLR(CLR), .CLK(CLK));
  Memory_Cell_8bits memory_cell_8bits_172 (
    .O(O), .Column(Col_6), .Row(Row_11), .NR_W(NR_W), .EN_O(EN_Output), .I(I), .CLR(CLR), .CLK(CLK));
  Memory_Cell_8bits memory_cell_8bits_173 (
    .O(O), .Column(Col_6), .Row(Row_12), .NR_W(NR_W), .EN_O(EN_Output), .I(I), .CLR(CLR), .CLK(CLK));
  Memory_Cell_8bits memory_cell_8bits_174 (
    .O(O), .Column(Col_6), .Row(Row_13), .NR_W(NR_W), .EN_O(EN_Output), .I(I), .CLR(CLR), .CLK(CLK));
  Memory_Cell_8bits memory_cell_8bits_175 (
    .O(O), .Column(Col_6), .Row(Row_14), .NR_W(NR_W), .EN_O(EN_Output), .I(I), .CLR(CLR), .CLK(CLK));
  Memory_Cell_8bits memory_cell_8bits_176 (
    .O(O), .Column(Col_6), .Row(Row_15), .NR_W(NR_W), .EN_O(EN_Output), .I(I), .CLR(CLR), .CLK(CLK));
  Memory_Cell_8bits memory_cell_8bits_177 (
    .O(O), .Column(Col_7), .Row(Row_8), .NR_W(NR_W), .EN_O(EN_Output), .I(I), .CLR(CLR), .CLK(CLK));
  Memory_Cell_8bits memory_cell_8bits_178 (
    .O(O), .Column(Col_7), .Row(Row_9), .NR_W(NR_W), .EN_O(EN_Output), .I(I), .CLR(CLR), .CLK(CLK));
  Memory_Cell_8bits memory_cell_8bits_179 (
    .O(O), .Column(Col_7), .Row(Row_10), .NR_W(NR_W), .EN_O(EN_Output), .I(I), .CLR(CLR), .CLK(CLK));
  Memory_Cell_8bits memory_cell_8bits_180 (
    .O(O), .Column(Col_7), .Row(Row_11), .NR_W(NR_W), .EN_O(EN_Output), .I(I), .CLR(CLR), .CLK(CLK));
  Memory_Cell_8bits memory_cell_8bits_181 (
    .O(O), .Column(Col_7), .Row(Row_12), .NR_W(NR_W), .EN_O(EN_Output), .I(I), .CLR(CLR), .CLK(CLK));
  Memory_Cell_8bits memory_cell_8bits_182 (
    .O(O), .Column(Col_7), .Row(Row_13), .NR_W(NR_W), .EN_O(EN_Output), .I(I), .CLR(CLR), .CLK(CLK));
  Memory_Cell_8bits memory_cell_8bits_183 (
    .O(O), .Column(Col_7), .Row(Row_14), .NR_W(NR_W), .EN_O(EN_Output), .I(I), .CLR(CLR), .CLK(CLK));
  Memory_Cell_8bits memory_cell_8bits_184 (
    .O(O), .Column(Col_7), .Row(Row_15), .NR_W(NR_W), .EN_O(EN_Output), .I(I), .CLR(CLR), .CLK(CLK));
  Memory_Cell_8bits memory_cell_8bits_185 (
    .O(O), .Column(Col_7), .Row(Row_0), .NR_W(NR_W), .EN_O(EN_Output), .I(I), .CLR(CLR), .CLK(CLK));
  Memory_Cell_8bits memory_cell_8bits_186 (
    .O(O), .Column(Col_7), .Row(Row_1), .NR_W(NR_W), .EN_O(EN_Output), .I(I), .CLR(CLR), .CLK(CLK));
  Memory_Cell_8bits memory_cell_8bits_187 (
    .O(O), .Column(Col_7), .Row(Row_2), .NR_W(NR_W), .EN_O(EN_Output), .I(I), .CLR(CLR), .CLK(CLK));
  Memory_Cell_8bits memory_cell_8bits_188 (
    .O(O), .Column(Col_7), .Row(Row_3), .NR_W(NR_W), .EN_O(EN_Output), .I(I), .CLR(CLR), .CLK(CLK));
  Memory_Cell_8bits memory_cell_8bits_189 (
    .O(O), .Column(Col_7), .Row(Row_4), .NR_W(NR_W), .EN_O(EN_Output), .I(I), .CLR(CLR), .CLK(CLK));
  Memory_Cell_8bits memory_cell_8bits_190 (
    .O(O), .Column(Col_7), .Row(Row_5), .NR_W(NR_W), .EN_O(EN_Output), .I(I), .CLR(CLR), .CLK(CLK));
  Memory_Cell_8bits memory_cell_8bits_191 (
    .O(O), .Column(Col_7), .Row(Row_6), .NR_W(NR_W), .EN_O(EN_Output), .I(I), .CLR(CLR), .CLK(CLK));
  Memory_Cell_8bits memory_cell_8bits_192 (
    .O(O), .Column(Col_7), .Row(Row_7), .NR_W(NR_W), .EN_O(EN_Output), .I(I), .CLR(CLR), .CLK(CLK));
  Memory_Cell_8bits memory_cell_8bits_193 (
    .O(O), .Column(Col_8), .Row(Row_0), .NR_W(NR_W), .EN_O(EN_Output), .I(I), .CLR(CLR), .CLK(CLK));
  Memory_Cell_8bits memory_cell_8bits_194 (
    .O(O), .Column(Col_8), .Row(Row_1), .NR_W(NR_W), .EN_O(EN_Output), .I(I), .CLR(CLR), .CLK(CLK));
  Memory_Cell_8bits memory_cell_8bits_195 (
    .O(O), .Column(Col_8), .Row(Row_2), .NR_W(NR_W), .EN_O(EN_Output), .I(I), .CLR(CLR), .CLK(CLK));
  Memory_Cell_8bits memory_cell_8bits_196 (
    .O(O), .Column(Col_8), .Row(Row_3), .NR_W(NR_W), .EN_O(EN_Output), .I(I), .CLR(CLR), .CLK(CLK));
  Memory_Cell_8bits memory_cell_8bits_197 (
    .O(O), .Column(Col_8), .Row(Row_4), .NR_W(NR_W), .EN_O(EN_Output), .I(I), .CLR(CLR), .CLK(CLK));
  Memory_Cell_8bits memory_cell_8bits_198 (
    .O(O), .Column(Col_8), .Row(Row_5), .NR_W(NR_W), .EN_O(EN_Output), .I(I), .CLR(CLR), .CLK(CLK));
  Memory_Cell_8bits memory_cell_8bits_199 (
    .O(O), .Column(Col_8), .Row(Row_6), .NR_W(NR_W), .EN_O(EN_Output), .I(I), .CLR(CLR), .CLK(CLK));
  Memory_Cell_8bits memory_cell_8bits_200 (
    .O(O), .Column(Col_8), .Row(Row_7), .NR_W(NR_W), .EN_O(EN_Output), .I(I), .CLR(CLR), .CLK(CLK));
  Memory_Cell_8bits memory_cell_8bits_201 (
    .O(O), .Column(Col_8), .Row(Row_8), .NR_W(NR_W), .EN_O(EN_Output), .I(I), .CLR(CLR), .CLK(CLK));
  Memory_Cell_8bits memory_cell_8bits_202 (
    .O(O), .Column(Col_8), .Row(Row_9), .NR_W(NR_W), .EN_O(EN_Output), .I(I), .CLR(CLR), .CLK(CLK));
  Memory_Cell_8bits memory_cell_8bits_203 (
    .O(O), .Column(Col_8), .Row(Row_10), .NR_W(NR_W), .EN_O(EN_Output), .I(I), .CLR(CLR), .CLK(CLK));
  Memory_Cell_8bits memory_cell_8bits_204 (
    .O(O), .Column(Col_8), .Row(Row_11), .NR_W(NR_W), .EN_O(EN_Output), .I(I), .CLR(CLR), .CLK(CLK));
  Memory_Cell_8bits memory_cell_8bits_205 (
    .O(O), .Column(Col_8), .Row(Row_12), .NR_W(NR_W), .EN_O(EN_Output), .I(I), .CLR(CLR), .CLK(CLK));
  Memory_Cell_8bits memory_cell_8bits_206 (
    .O(O), .Column(Col_8), .Row(Row_13), .NR_W(NR_W), .EN_O(EN_Output), .I(I), .CLR(CLR), .CLK(CLK));
  Memory_Cell_8bits memory_cell_8bits_207 (
    .O(O), .Column(Col_8), .Row(Row_14), .NR_W(NR_W), .EN_O(EN_Output), .I(I), .CLR(CLR), .CLK(CLK));
  Memory_Cell_8bits memory_cell_8bits_208 (
    .O(O), .Column(Col_8), .Row(Row_15), .NR_W(NR_W), .EN_O(EN_Output), .I(I), .CLR(CLR), .CLK(CLK));
  Memory_Cell_8bits memory_cell_8bits_209 (
    .O(O), .Column(Col_9), .Row(Row_0), .NR_W(NR_W), .EN_O(EN_Output), .I(I), .CLR(CLR), .CLK(CLK));
  Memory_Cell_8bits memory_cell_8bits_210 (
    .O(O), .Column(Col_9), .Row(Row_1), .NR_W(NR_W), .EN_O(EN_Output), .I(I), .CLR(CLR), .CLK(CLK));
  Memory_Cell_8bits memory_cell_8bits_211 (
    .O(O), .Column(Col_9), .Row(Row_2), .NR_W(NR_W), .EN_O(EN_Output), .I(I), .CLR(CLR), .CLK(CLK));
  Memory_Cell_8bits memory_cell_8bits_212 (
    .O(O), .Column(Col_9), .Row(Row_3), .NR_W(NR_W), .EN_O(EN_Output), .I(I), .CLR(CLR), .CLK(CLK));
  Memory_Cell_8bits memory_cell_8bits_213 (
    .O(O), .Column(Col_9), .Row(Row_4), .NR_W(NR_W), .EN_O(EN_Output), .I(I), .CLR(CLR), .CLK(CLK));
  Memory_Cell_8bits memory_cell_8bits_214 (
    .O(O), .Column(Col_9), .Row(Row_5), .NR_W(NR_W), .EN_O(EN_Output), .I(I), .CLR(CLR), .CLK(CLK));
  Memory_Cell_8bits memory_cell_8bits_215 (
    .O(O), .Column(Col_9), .Row(Row_6), .NR_W(NR_W), .EN_O(EN_Output), .I(I), .CLR(CLR), .CLK(CLK));
  Memory_Cell_8bits memory_cell_8bits_216 (
    .O(O), .Column(Col_9), .Row(Row_7), .NR_W(NR_W), .EN_O(EN_Output), .I(I), .CLR(CLR), .CLK(CLK));
  Memory_Cell_8bits memory_cell_8bits_217 (
    .O(O), .Column(Col_9), .Row(Row_8), .NR_W(NR_W), .EN_O(EN_Output), .I(I), .CLR(CLR), .CLK(CLK));
  Memory_Cell_8bits memory_cell_8bits_218 (
    .O(O), .Column(Col_9), .Row(Row_9), .NR_W(NR_W), .EN_O(EN_Output), .I(I), .CLR(CLR), .CLK(CLK));
  Memory_Cell_8bits memory_cell_8bits_219 (
    .O(O), .Column(Col_9), .Row(Row_10), .NR_W(NR_W), .EN_O(EN_Output), .I(I), .CLR(CLR), .CLK(CLK));
  Memory_Cell_8bits memory_cell_8bits_220 (
    .O(O), .Column(Col_9), .Row(Row_11), .NR_W(NR_W), .EN_O(EN_Output), .I(I), .CLR(CLR), .CLK(CLK));
  Memory_Cell_8bits memory_cell_8bits_221 (
    .O(O), .Column(Col_9), .Row(Row_12), .NR_W(NR_W), .EN_O(EN_Output), .I(I), .CLR(CLR), .CLK(CLK));
  Memory_Cell_8bits memory_cell_8bits_222 (
    .O(O), .Column(Col_9), .Row(Row_13), .NR_W(NR_W), .EN_O(EN_Output), .I(I), .CLR(CLR), .CLK(CLK));
  Memory_Cell_8bits memory_cell_8bits_223 (
    .O(O), .Column(Col_9), .Row(Row_14), .NR_W(NR_W), .EN_O(EN_Output), .I(I), .CLR(CLR), .CLK(CLK));
  Memory_Cell_8bits memory_cell_8bits_224 (
    .O(O), .Column(Col_9), .Row(Row_15), .NR_W(NR_W), .EN_O(EN_Output), .I(I), .CLR(CLR), .CLK(CLK));
  Memory_Cell_8bits memory_cell_8bits_225 (
    .O(O), .Column(Col_10), .Row(Row_0), .NR_W(NR_W), .EN_O(EN_Output), .I(I), .CLR(CLR), .CLK(CLK));
  Memory_Cell_8bits memory_cell_8bits_226 (
    .O(O), .Column(Col_10), .Row(Row_1), .NR_W(NR_W), .EN_O(EN_Output), .I(I), .CLR(CLR), .CLK(CLK));
  Memory_Cell_8bits memory_cell_8bits_227 (
    .O(O), .Column(Col_10), .Row(Row_2), .NR_W(NR_W), .EN_O(EN_Output), .I(I), .CLR(CLR), .CLK(CLK));
  Memory_Cell_8bits memory_cell_8bits_228 (
    .O(O), .Column(Col_10), .Row(Row_3), .NR_W(NR_W), .EN_O(EN_Output), .I(I), .CLR(CLR), .CLK(CLK));
  Memory_Cell_8bits memory_cell_8bits_229 (
    .O(O), .Column(Col_10), .Row(Row_4), .NR_W(NR_W), .EN_O(EN_Output), .I(I), .CLR(CLR), .CLK(CLK));
  Memory_Cell_8bits memory_cell_8bits_230 (
    .O(O), .Column(Col_10), .Row(Row_5), .NR_W(NR_W), .EN_O(EN_Output), .I(I), .CLR(CLR), .CLK(CLK));
  Memory_Cell_8bits memory_cell_8bits_231 (
    .O(O), .Column(Col_10), .Row(Row_6), .NR_W(NR_W), .EN_O(EN_Output), .I(I), .CLR(CLR), .CLK(CLK));
  Memory_Cell_8bits memory_cell_8bits_232 (
    .O(O), .Column(Col_10), .Row(Row_7), .NR_W(NR_W), .EN_O(EN_Output), .I(I), .CLR(CLR), .CLK(CLK));
  Memory_Cell_8bits memory_cell_8bits_233 (
    .O(O), .Column(Col_10), .Row(Row_8), .NR_W(NR_W), .EN_O(EN_Output), .I(I), .CLR(CLR), .CLK(CLK));
  Memory_Cell_8bits memory_cell_8bits_234 (
    .O(O), .Column(Col_10), .Row(Row_9), .NR_W(NR_W), .EN_O(EN_Output), .I(I), .CLR(CLR), .CLK(CLK));
  Memory_Cell_8bits memory_cell_8bits_235 (
    .O(O), .Column(Col_10), .Row(Row_10), .NR_W(NR_W), .EN_O(EN_Output), .I(I), .CLR(CLR), .CLK(CLK));
  Memory_Cell_8bits memory_cell_8bits_236 (
    .O(O), .Column(Col_10), .Row(Row_11), .NR_W(NR_W), .EN_O(EN_Output), .I(I), .CLR(CLR), .CLK(CLK));
  Memory_Cell_8bits memory_cell_8bits_237 (
    .O(O), .Column(Col_10), .Row(Row_12), .NR_W(NR_W), .EN_O(EN_Output), .I(I), .CLR(CLR), .CLK(CLK));
  Memory_Cell_8bits memory_cell_8bits_238 (
    .O(O), .Column(Col_10), .Row(Row_13), .NR_W(NR_W), .EN_O(EN_Output), .I(I), .CLR(CLR), .CLK(CLK));
  Memory_Cell_8bits memory_cell_8bits_239 (
    .O(O), .Column(Col_10), .Row(Row_14), .NR_W(NR_W), .EN_O(EN_Output), .I(I), .CLR(CLR), .CLK(CLK));
  Memory_Cell_8bits memory_cell_8bits_240 (
    .O(O), .Column(Col_10), .Row(Row_15), .NR_W(NR_W), .EN_O(EN_Output), .I(I), .CLR(CLR), .CLK(CLK));
  Memory_Cell_8bits memory_cell_8bits_241 (
    .O(O), .Column(Col_11), .Row(Row_0), .NR_W(NR_W), .EN_O(EN_Output), .I(I), .CLR(CLR), .CLK(CLK));
  Memory_Cell_8bits memory_cell_8bits_242 (
    .O(O), .Column(Col_11), .Row(Row_1), .NR_W(NR_W), .EN_O(EN_Output), .I(I), .CLR(CLR), .CLK(CLK));
  Memory_Cell_8bits memory_cell_8bits_243 (
    .O(O), .Column(Col_11), .Row(Row_2), .NR_W(NR_W), .EN_O(EN_Output), .I(I), .CLR(CLR), .CLK(CLK));
  Memory_Cell_8bits memory_cell_8bits_244 (
    .O(O), .Column(Col_11), .Row(Row_3), .NR_W(NR_W), .EN_O(EN_Output), .I(I), .CLR(CLR), .CLK(CLK));
  Memory_Cell_8bits memory_cell_8bits_245 (
    .O(O), .Column(Col_11), .Row(Row_4), .NR_W(NR_W), .EN_O(EN_Output), .I(I), .CLR(CLR), .CLK(CLK));
  Memory_Cell_8bits memory_cell_8bits_246 (
    .O(O), .Column(Col_11), .Row(Row_5), .NR_W(NR_W), .EN_O(EN_Output), .I(I), .CLR(CLR), .CLK(CLK));
  Memory_Cell_8bits memory_cell_8bits_247 (
    .O(O), .Column(Col_11), .Row(Row_6), .NR_W(NR_W), .EN_O(EN_Output), .I(I), .CLR(CLR), .CLK(CLK));
  Memory_Cell_8bits memory_cell_8bits_248 (
    .O(O), .Column(Col_11), .Row(Row_7), .NR_W(NR_W), .EN_O(EN_Output), .I(I), .CLR(CLR), .CLK(CLK));
  Memory_Cell_8bits memory_cell_8bits_249 (
    .O(O), .Column(Col_11), .Row(Row_8), .NR_W(NR_W), .EN_O(EN_Output), .I(I), .CLR(CLR), .CLK(CLK));
  Memory_Cell_8bits memory_cell_8bits_250 (
    .O(O), .Column(Col_11), .Row(Row_9), .NR_W(NR_W), .EN_O(EN_Output), .I(I), .CLR(CLR), .CLK(CLK));
  Memory_Cell_8bits memory_cell_8bits_251 (
    .O(O), .Column(Col_11), .Row(Row_10), .NR_W(NR_W), .EN_O(EN_Output), .I(I), .CLR(CLR), .CLK(CLK));
  Memory_Cell_8bits memory_cell_8bits_252 (
    .O(O), .Column(Col_11), .Row(Row_11), .NR_W(NR_W), .EN_O(EN_Output), .I(I), .CLR(CLR), .CLK(CLK));
  Memory_Cell_8bits memory_cell_8bits_253 (
    .O(O), .Column(Col_11), .Row(Row_12), .NR_W(NR_W), .EN_O(EN_Output), .I(I), .CLR(CLR), .CLK(CLK));
  Memory_Cell_8bits memory_cell_8bits_254 (
    .O(O), .Column(Col_11), .Row(Row_13), .NR_W(NR_W), .EN_O(EN_Output), .I(I), .CLR(CLR), .CLK(CLK));
  Memory_Cell_8bits memory_cell_8bits_255 (
    .O(O), .Column(Col_11), .Row(Row_14), .NR_W(NR_W), .EN_O(EN_Output), .I(I), .CLR(CLR), .CLK(CLK));
  Memory_Cell_8bits memory_cell_8bits_256 (
    .O(O), .Column(Col_11), .Row(Row_15), .NR_W(NR_W), .EN_O(EN_Output), .I(I), .CLR(CLR), .CLK(CLK));
  Memory_Cell_8bits memory_cell_8bits_257 (
    .O(O), .Column(Col_12), .Row(Row_0), .NR_W(NR_W), .EN_O(EN_Output), .I(I), .CLR(CLR), .CLK(CLK));
  Memory_Cell_8bits memory_cell_8bits_258 (
    .O(O), .Column(Col_12), .Row(Row_1), .NR_W(NR_W), .EN_O(EN_Output), .I(I), .CLR(CLR), .CLK(CLK));
  Memory_Cell_8bits memory_cell_8bits_259 (
    .O(O), .Column(Col_12), .Row(Row_2), .NR_W(NR_W), .EN_O(EN_Output), .I(I), .CLR(CLR), .CLK(CLK));
  Memory_Cell_8bits memory_cell_8bits_260 (
    .O(O), .Column(Col_12), .Row(Row_3), .NR_W(NR_W), .EN_O(EN_Output), .I(I), .CLR(CLR), .CLK(CLK));
  Memory_Cell_8bits memory_cell_8bits_261 (
    .O(O), .Column(Col_12), .Row(Row_4), .NR_W(NR_W), .EN_O(EN_Output), .I(I), .CLR(CLR), .CLK(CLK));
  Memory_Cell_8bits memory_cell_8bits_262 (
    .O(O), .Column(Col_12), .Row(Row_5), .NR_W(NR_W), .EN_O(EN_Output), .I(I), .CLR(CLR), .CLK(CLK));
  Memory_Cell_8bits memory_cell_8bits_263 (
    .O(O), .Column(Col_12), .Row(Row_6), .NR_W(NR_W), .EN_O(EN_Output), .I(I), .CLR(CLR), .CLK(CLK));
  Memory_Cell_8bits memory_cell_8bits_264 (
    .O(O), .Column(Col_12), .Row(Row_7), .NR_W(NR_W), .EN_O(EN_Output), .I(I), .CLR(CLR), .CLK(CLK));
  Memory_Cell_8bits memory_cell_8bits_265 (
    .O(O), .Column(Col_12), .Row(Row_8), .NR_W(NR_W), .EN_O(EN_Output), .I(I), .CLR(CLR), .CLK(CLK));
  Memory_Cell_8bits memory_cell_8bits_266 (
    .O(O), .Column(Col_12), .Row(Row_9), .NR_W(NR_W), .EN_O(EN_Output), .I(I), .CLR(CLR), .CLK(CLK));
  Memory_Cell_8bits memory_cell_8bits_267 (
    .O(O), .Column(Col_12), .Row(Row_10), .NR_W(NR_W), .EN_O(EN_Output), .I(I), .CLR(CLR), .CLK(CLK));
  Memory_Cell_8bits memory_cell_8bits_268 (
    .O(O), .Column(Col_12), .Row(Row_11), .NR_W(NR_W), .EN_O(EN_Output), .I(I), .CLR(CLR), .CLK(CLK));
  Memory_Cell_8bits memory_cell_8bits_269 (
    .O(O), .Column(Col_12), .Row(Row_12), .NR_W(NR_W), .EN_O(EN_Output), .I(I), .CLR(CLR), .CLK(CLK));
  Memory_Cell_8bits memory_cell_8bits_270 (
    .O(O), .Column(Col_12), .Row(Row_13), .NR_W(NR_W), .EN_O(EN_Output), .I(I), .CLR(CLR), .CLK(CLK));
  Memory_Cell_8bits memory_cell_8bits_271 (
    .O(O), .Column(Col_12), .Row(Row_14), .NR_W(NR_W), .EN_O(EN_Output), .I(I), .CLR(CLR), .CLK(CLK));
  Memory_Cell_8bits memory_cell_8bits_272 (
    .O(O), .Column(Col_12), .Row(Row_15), .NR_W(NR_W), .EN_O(EN_Output), .I(I), .CLR(CLR), .CLK(CLK));
  Memory_Cell_8bits memory_cell_8bits_273 (
    .O(O), .Column(Col_13), .Row(Row_0), .NR_W(NR_W), .EN_O(EN_Output), .I(I), .CLR(CLR), .CLK(CLK));
  Memory_Cell_8bits memory_cell_8bits_274 (
    .O(O), .Column(Col_13), .Row(Row_1), .NR_W(NR_W), .EN_O(EN_Output), .I(I), .CLR(CLR), .CLK(CLK));
  Memory_Cell_8bits memory_cell_8bits_275 (
    .O(O), .Column(Col_13), .Row(Row_2), .NR_W(NR_W), .EN_O(EN_Output), .I(I), .CLR(CLR), .CLK(CLK));
  Memory_Cell_8bits memory_cell_8bits_276 (
    .O(O), .Column(Col_13), .Row(Row_3), .NR_W(NR_W), .EN_O(EN_Output), .I(I), .CLR(CLR), .CLK(CLK));
  Memory_Cell_8bits memory_cell_8bits_277 (
    .O(O), .Column(Col_13), .Row(Row_4), .NR_W(NR_W), .EN_O(EN_Output), .I(I), .CLR(CLR), .CLK(CLK));
  Memory_Cell_8bits memory_cell_8bits_278 (
    .O(O), .Column(Col_13), .Row(Row_5), .NR_W(NR_W), .EN_O(EN_Output), .I(I), .CLR(CLR), .CLK(CLK));
  Memory_Cell_8bits memory_cell_8bits_279 (
    .O(O), .Column(Col_13), .Row(Row_6), .NR_W(NR_W), .EN_O(EN_Output), .I(I), .CLR(CLR), .CLK(CLK));
  Memory_Cell_8bits memory_cell_8bits_280 (
    .O(O), .Column(Col_13), .Row(Row_7), .NR_W(NR_W), .EN_O(EN_Output), .I(I), .CLR(CLR), .CLK(CLK));
  Memory_Cell_8bits memory_cell_8bits_281 (
    .O(O), .Column(Col_13), .Row(Row_8), .NR_W(NR_W), .EN_O(EN_Output), .I(I), .CLR(CLR), .CLK(CLK));
  Memory_Cell_8bits memory_cell_8bits_282 (
    .O(O), .Column(Col_13), .Row(Row_9), .NR_W(NR_W), .EN_O(EN_Output), .I(I), .CLR(CLR), .CLK(CLK));
  Memory_Cell_8bits memory_cell_8bits_283 (
    .O(O), .Column(Col_13), .Row(Row_10), .NR_W(NR_W), .EN_O(EN_Output), .I(I), .CLR(CLR), .CLK(CLK));
  Memory_Cell_8bits memory_cell_8bits_284 (
    .O(O), .Column(Col_13), .Row(Row_11), .NR_W(NR_W), .EN_O(EN_Output), .I(I), .CLR(CLR), .CLK(CLK));
  Memory_Cell_8bits memory_cell_8bits_285 (
    .O(O), .Column(Col_13), .Row(Row_12), .NR_W(NR_W), .EN_O(EN_Output), .I(I), .CLR(CLR), .CLK(CLK));
  Memory_Cell_8bits memory_cell_8bits_286 (
    .O(O), .Column(Col_13), .Row(Row_13), .NR_W(NR_W), .EN_O(EN_Output), .I(I), .CLR(CLR), .CLK(CLK));
  Memory_Cell_8bits memory_cell_8bits_287 (
    .O(O), .Column(Col_13), .Row(Row_14), .NR_W(NR_W), .EN_O(EN_Output), .I(I), .CLR(CLR), .CLK(CLK));
  Memory_Cell_8bits memory_cell_8bits_288 (
    .O(O), .Column(Col_13), .Row(Row_15), .NR_W(NR_W), .EN_O(EN_Output), .I(I), .CLR(CLR), .CLK(CLK));
  Memory_Cell_8bits memory_cell_8bits_289 (
    .O(O), .Column(Col_14), .Row(Row_0), .NR_W(NR_W), .EN_O(EN_Output), .I(I), .CLR(CLR), .CLK(CLK));
  Memory_Cell_8bits memory_cell_8bits_290 (
    .O(O), .Column(Col_14), .Row(Row_1), .NR_W(NR_W), .EN_O(EN_Output), .I(I), .CLR(CLR), .CLK(CLK));
  Memory_Cell_8bits memory_cell_8bits_291 (
    .O(O), .Column(Col_14), .Row(Row_2), .NR_W(NR_W), .EN_O(EN_Output), .I(I), .CLR(CLR), .CLK(CLK));
  Memory_Cell_8bits memory_cell_8bits_292 (
    .O(O), .Column(Col_14), .Row(Row_3), .NR_W(NR_W), .EN_O(EN_Output), .I(I), .CLR(CLR), .CLK(CLK));
  Memory_Cell_8bits memory_cell_8bits_293 (
    .O(O), .Column(Col_14), .Row(Row_4), .NR_W(NR_W), .EN_O(EN_Output), .I(I), .CLR(CLR), .CLK(CLK));
  Memory_Cell_8bits memory_cell_8bits_294 (
    .O(O), .Column(Col_14), .Row(Row_5), .NR_W(NR_W), .EN_O(EN_Output), .I(I), .CLR(CLR), .CLK(CLK));
  Memory_Cell_8bits memory_cell_8bits_295 (
    .O(O), .Column(Col_14), .Row(Row_6), .NR_W(NR_W), .EN_O(EN_Output), .I(I), .CLR(CLR), .CLK(CLK));
  Memory_Cell_8bits memory_cell_8bits_296 (
    .O(O), .Column(Col_14), .Row(Row_7), .NR_W(NR_W), .EN_O(EN_Output), .I(I), .CLR(CLR), .CLK(CLK));
  Memory_Cell_8bits memory_cell_8bits_297 (
    .O(O), .Column(Col_14), .Row(Row_8), .NR_W(NR_W), .EN_O(EN_Output), .I(I), .CLR(CLR), .CLK(CLK));
  Memory_Cell_8bits memory_cell_8bits_298 (
    .O(O), .Column(Col_14), .Row(Row_9), .NR_W(NR_W), .EN_O(EN_Output), .I(I), .CLR(CLR), .CLK(CLK));
  Memory_Cell_8bits memory_cell_8bits_299 (
    .O(O), .Column(Col_14), .Row(Row_10), .NR_W(NR_W), .EN_O(EN_Output), .I(I), .CLR(CLR), .CLK(CLK));
  Memory_Cell_8bits memory_cell_8bits_300 (
    .O(O), .Column(Col_14), .Row(Row_11), .NR_W(NR_W), .EN_O(EN_Output), .I(I), .CLR(CLR), .CLK(CLK));
  Memory_Cell_8bits memory_cell_8bits_301 (
    .O(O), .Column(Col_14), .Row(Row_12), .NR_W(NR_W), .EN_O(EN_Output), .I(I), .CLR(CLR), .CLK(CLK));
  Memory_Cell_8bits memory_cell_8bits_302 (
    .O(O), .Column(Col_14), .Row(Row_13), .NR_W(NR_W), .EN_O(EN_Output), .I(I), .CLR(CLR), .CLK(CLK));
  Memory_Cell_8bits memory_cell_8bits_303 (
    .O(O), .Column(Col_14), .Row(Row_14), .NR_W(NR_W), .EN_O(EN_Output), .I(I), .CLR(CLR), .CLK(CLK));
  Memory_Cell_8bits memory_cell_8bits_304 (
    .O(O), .Column(Col_14), .Row(Row_15), .NR_W(NR_W), .EN_O(EN_Output), .I(I), .CLR(CLR), .CLK(CLK));
  Memory_Cell_8bits memory_cell_8bits_305 (
    .O(O), .Column(Col_15), .Row(Row_8), .NR_W(NR_W), .EN_O(EN_Output), .I(I), .CLR(CLR), .CLK(CLK));
  Memory_Cell_8bits memory_cell_8bits_306 (
    .O(O), .Column(Col_15), .Row(Row_9), .NR_W(NR_W), .EN_O(EN_Output), .I(I), .CLR(CLR), .CLK(CLK));
  Memory_Cell_8bits memory_cell_8bits_307 (
    .O(O), .Column(Col_15), .Row(Row_10), .NR_W(NR_W), .EN_O(EN_Output), .I(I), .CLR(CLR), .CLK(CLK));
  Memory_Cell_8bits memory_cell_8bits_308 (
    .O(O), .Column(Col_15), .Row(Row_11), .NR_W(NR_W), .EN_O(EN_Output), .I(I), .CLR(CLR), .CLK(CLK));
  Memory_Cell_8bits memory_cell_8bits_309 (
    .O(O), .Column(Col_15), .Row(Row_12), .NR_W(NR_W), .EN_O(EN_Output), .I(I), .CLR(CLR), .CLK(CLK));
  Memory_Cell_8bits memory_cell_8bits_310 (
    .O(O), .Column(Col_15), .Row(Row_13), .NR_W(NR_W), .EN_O(EN_Output), .I(I), .CLR(CLR), .CLK(CLK));
  Memory_Cell_8bits memory_cell_8bits_311 (
    .O(O), .Column(Col_15), .Row(Row_14), .NR_W(NR_W), .EN_O(EN_Output), .I(I), .CLR(CLR), .CLK(CLK));
  Memory_Cell_8bits memory_cell_8bits_312 (
    .O(O), .Column(Col_15), .Row(Row_15), .NR_W(NR_W), .EN_O(EN_Output), .I(I), .CLR(CLR), .CLK(CLK));
  Memory_Cell_8bits memory_cell_8bits_313 (
    .O(O), .Column(Col_15), .Row(Row_0), .NR_W(NR_W), .EN_O(EN_Output), .I(I), .CLR(CLR), .CLK(CLK));
  Memory_Cell_8bits memory_cell_8bits_314 (
    .O(O), .Column(Col_15), .Row(Row_1), .NR_W(NR_W), .EN_O(EN_Output), .I(I), .CLR(CLR), .CLK(CLK));
  Memory_Cell_8bits memory_cell_8bits_315 (
    .O(O), .Column(Col_15), .Row(Row_2), .NR_W(NR_W), .EN_O(EN_Output), .I(I), .CLR(CLR), .CLK(CLK));
  Memory_Cell_8bits memory_cell_8bits_316 (
    .O(O), .Column(Col_15), .Row(Row_3), .NR_W(NR_W), .EN_O(EN_Output), .I(I), .CLR(CLR), .CLK(CLK));
  Memory_Cell_8bits memory_cell_8bits_317 (
    .O(O), .Column(Col_15), .Row(Row_4), .NR_W(NR_W), .EN_O(EN_Output), .I(I), .CLR(CLR), .CLK(CLK));
  Memory_Cell_8bits memory_cell_8bits_318 (
    .O(O), .Column(Col_15), .Row(Row_5), .NR_W(NR_W), .EN_O(EN_Output), .I(I), .CLR(CLR), .CLK(CLK));
  Memory_Cell_8bits memory_cell_8bits_319 (
    .O(O), .Column(Col_15), .Row(Row_6), .NR_W(NR_W), .EN_O(EN_Output), .I(I), .CLR(CLR), .CLK(CLK));
  Memory_Cell_8bits memory_cell_8bits_320 (
    .O(O), .Column(Col_15), .Row(Row_7), .NR_W(NR_W), .EN_O(EN_Output), .I(I), .CLR(CLR), .CLK(CLK));
  Decoder #(.select(4)) decoder_1 (
    .out0(Col_0), .out1(Col_1), .out2(Col_2), .out3(Col_3), .out4(Col_4), .out5(Col_5), .out6(Col_6),
    .out7(Col_7), .out8(Col_8), .out9(Col_9), .out10(Col_10), .out11(Col_11), .out12(Col_12), .out13(Col_13),
    .out14(Col_14), .out15(Col_15), .sel(Addrs[7:4]), .en(Enable));
  Decoder #(.select(4)) decoder_2 (
    .out0(Row_0), .out1(Row_1), .out2(Row_2), .out3(Row_3), .out4(Row_4), .out5(Row_5), .out6(Row_6),
    .out7(Row_7), .out8(Row_8), .out9(Row_9), .out10(Row_10), .out11(Row_11), .out12(Row_12), .out13(Row_13),
    .out14(Row_14), .out15(Row_15), .sel(Addrs[3:0]), .en(Enable));

  // Other names for the same wires on the sheet: EN_Cell_O = EN_Output; EN_RAM = Enable
endmodule

module RAM_MAR_MDR (
  input  [7:0] BUS_I,
  input  NR_W_RAM,
  input  EN_MAR,
  input  EN_RAM_I,
  input  CLR_MAR,
  input  EN_RAM_O,
  input  Select_MDR_I,
  input  Select_MDR_O,
  input  [7:0] Upper_BUS_I,
  input  EN_MDR_I,
  input  EN_MDR_O,
  input  CLR_RAM,
  input  CLR_MDR,
  input  CLK,
  output [7:0] BUS_O_Upper,
  output [7:0] BUS_O
);

  wire [7:0] Data_O_RAM, mar_1_addrs_o, ram_256bytes_1_o, ram_256bytes_1_o_upper;

  MAR mar_1 (.Addrs_O(mar_1_addrs_o), .Addrs_I(BUS_I), .CLR(CLR_MAR), .CLK(CLK), .EN(EN_MAR));
  RAM_256bytes ram_256bytes_1 (
    .O(ram_256bytes_1_o), .O_Upper(ram_256bytes_1_o_upper), .I(Data_O_RAM), .I_Upper(Upper_BUS_I),
    .Enable(EN_RAM_I), .EN_Output(EN_RAM_O), .NR_W(NR_W_RAM), .CLR(CLR_RAM), .CLK(CLK), .Addrs(mar_1_addrs_o));
  MDR mdr_1 (
    .Data_O_RAM(Data_O_RAM), .Data_O_BUS(BUS_O), .Data_O_BUS_Upper(BUS_O_Upper), .EN_I(EN_MDR_I),
    .Select_O(Select_MDR_O), .EN_O(EN_MDR_O), .Data_I_BUS(BUS_I), .Data_I_RAM(ram_256bytes_1_o),
    .Data_I_RAM_Upper(ram_256bytes_1_o_upper), .Select_I(Select_MDR_I), .CLR(CLR_MDR), .CLK(CLK));
endmodule

module Ring_Counter (
  input  CLK,
  input  RST,
  output O0,
  output O1,
  output O2,
  output O3,
  output O4,
  output O5,
  output O6,
  output O7
);

  wire A0, A1, A2, and_2_out, NA0, NA1, NA2, not_1_out, NRST, T2;

  and and_1 (T2, A1, A0);
  not not_1 (not_1_out, CLK);
  T_Flip_Flop T0 (.T(1'b1), .clk(not_1_out), .Q(A0), .Qn(NA0), .reset(RST));  // open: preset
  T_Flip_Flop T1 (.T(A0), .clk(not_1_out), .Q(A1), .Qn(NA1), .reset(RST));  // open: preset
  T_Flip_Flop u_T2 (.T(T2), .clk(not_1_out), .Q(A2), .Qn(NA2), .reset(RST));  // open: preset
  not not_2 (NRST, RST);
  and and_2 (and_2_out, NA2, NA1, NA0);
  and and_3 (O1, NA2, NA1, A0);
  and and_4 (O2, NA2, A1, NA0);
  and and_5 (O3, NA2, A1, A0);
  and and_6 (O4, A2, NA1, NA0);
  and and_7 (O5, A2, NA1, A0);
  and and_8 (O6, A2, A1, NA0);
  and and_9 (O7, A2, A1, A0);
  and and_10 (O0, and_2_out, NRST);

  // Other names for the same wires on the sheet: T1 = A0
endmodule

module Control_Unit (
  input  CLK,
  input  Master_Reset,
  input  [7:0] IR_Upper_I,
  input  [7:0] IR_I,
  input  STATUS_Cout_NBout,
  input  STATUS_N,
  input  STATUS_Z,
  output HALT,
  output IR_CLR,
  output REG_0_CLR,
  output REG_1_CLR,
  output [7:0] BUS_O,
  output REG_2_CLR,
  output REG_3_CLR,
  output REG_4_CLR,
  output ALU_A_I_CLR,
  output ACC_CLR,
  output PC_EN_O,
  output STATUS_CLR,
  output MAR_CLR,
  output MDR_CLR,
  output RAM_CLR,
  output PC_Reset,
  output IR_EN_I,
  output IR_EN_O,
  output [4:0] ALU_OPCODE,
  output ALU_A_I_EN,
  output ALU_EN,
  output STATUS_EN,
  output ALU_SUBTRACT,
  output Cout_NBout,
  output PC_Load,
  output MAR_EN,
  output ACC_EN_BUS_O,
  output MDR_EN_I,
  output MDR_SEL_I,
  output REG_0_EN_O,
  output RAM_EN_O,
  output REG_1_EN_O,
  output REG_2_EN_O,
  output REG_3_EN_O,
  output REG_4_EN_O,
  output PC_Count,
  output INPUT_REG_EN_O,
  output ACC_EN_I,
  output ACC_SELECT_I,
  output RAM_EN_I,
  output REG_0_EN_I,
  output RAM_NR_W,
  output REG_1_EN_I,
  output MDR_SEL_O,
  output REG_2_EN_I,
  output REG_3_EN_I,
  output MDR_EN_O,
  output REG_4_EN_I,
  output OUTPUT_REG_EN_I
);

  wire ACC_000, ACC_EN_BUS_O_t, ACC_EN_I_t, ACC_SELECT_I_t, and_2_out, and_3_out, and_4_out, and_6_out,
       and_14_out, and_15_out, and_16_out, and_24_out, and_25_out, and_26_out, and_27_out, and_28_out,
       and_29_out, and_30_out, and_31_out, and_32_out, and_33_out, and_34_out, and_35_out, and_36_out,
       and_37_out, and_39_out, and_40_out, and_43_out, and_44_out, and_45_out, and_46_out, and_47_out,
       and_48_out, INPUT_REG_110, INPUT_REG_EN_O_t, INSTRUCTION_0, INSTRUCTION_1, INSTRUCTION_2,
       INSTRUCTION_3, INSTRUCTION_4, INSTRUCTION_5, INSTRUCTION_6, INSTRUCTION_7, INSTRUCTION_8,
       INSTRUCTION_9, INSTRUCTION_10, INSTRUCTION_11, INSTRUCTION_12, INSTRUCTION_13, INSTRUCTION_14,
       INSTRUCTION_15, INSTRUCTION_16, INSTRUCTION_17, INSTRUCTION_18, INSTRUCTION_19, INSTRUCTION_20,
       INSTRUCTION_21, INSTRUCTION_22, INSTRUCTION_23, INSTRUCTION_24, INSTRUCTION_26, INSTRUCTION_27,
       INSTRUCTION_28, INSTRUCTION_29, INSTRUCTION_30, INSTRUCTION_31, MDR_EN_I_t, not_1_out, or_2_out,
       or_7_out, or_8_out, or_9_out, or_11_out, or_19_out, or_27_out, OUTPUT_REG_111, OUTPUT_REG_EN_I_t,
       PC_RESET_t, REG0_001, REG1_010, REG2_011, REG3_100, REG4_101, REG_0_EN_I_t, REG_0_EN_O_t,
       REG_1_EN_I_t, REG_1_EN_O_t, REG_2_EN_I_t, REG_2_EN_O_t, REG_3_EN_I_t, REG_3_EN_O_t, REG_4_EN_I_t,
       REG_4_EN_O_t, Ring_Counter_5, Ring_Counter_6, Ring_Counter_7;
  wire [2:0] Output_Selector;
  wire [7:0] Addrs_or_Literal;

  or or_1 (PC_Reset, Master_Reset, PC_RESET_t);
  Ring_Counter ring_counter_1 (
    .O4(ALU_A_I_EN), .O5(Ring_Counter_5), .O6(Ring_Counter_6), .O7(Ring_Counter_7), .O0(PC_EN_O),
    .O1(MDR_EN_I_t), .O2(IR_EN_I), .O3(IR_EN_O), .CLK(CLK), .RST(Master_Reset));
  or or_2 (or_2_out, INSTRUCTION_12, INSTRUCTION_0, INSTRUCTION_2, INSTRUCTION_4, INSTRUCTION_8, INSTRUCTION_11, INSTRUCTION_13, INSTRUCTION_15, INSTRUCTION_16, INSTRUCTION_17, INSTRUCTION_18, INSTRUCTION_19, INSTRUCTION_20, INSTRUCTION_30);
  and and_1 (ACC_SELECT_I_t, Ring_Counter_5, INSTRUCTION_20);
  and and_2 (and_2_out, Ring_Counter_7, INSTRUCTION_22);
  and and_3 (and_3_out, ACC_000, and_2_out);
  or or_3 (ACC_EN_I, ACC_SELECT_I_t, ACC_EN_I_t, and_3_out);
  or or_4 (ACC_SELECT_I, and_2_out, ACC_SELECT_I_t);
  and and_4 (and_4_out, INSTRUCTION_22, Ring_Counter_6);
  and and_5 (MDR_SEL_O, Ring_Counter_7, INSTRUCTION_21);
  and and_6 (and_6_out, Ring_Counter_7, INSTRUCTION_22);
  Register_8bit IR_UPPER_I_REG (
    .O({ALU_OPCODE, Output_Selector}), .I(IR_Upper_I), .Enable(IR_EN_O), .CLK(CLK), .CLR(Master_Reset));
  Register_8bit IR_I_REG (.O(Addrs_or_Literal), .I(IR_I), .Enable(IR_EN_O), .CLK(CLK), .CLR(Master_Reset));
  or or_5 (RAM_EN_I, and_4_out, MDR_SEL_O, MDR_EN_I_t);
  or or_6 (MDR_EN_O, and_6_out, IR_EN_I);
  and and_7 (REG_0_EN_I_t, Ring_Counter_6, or_2_out, REG0_001);
  and and_8 (REG_1_EN_I_t, Ring_Counter_6, or_2_out, REG1_010);
  and and_9 (REG_2_EN_I_t, Ring_Counter_6, or_2_out, REG2_011);
  and and_10 (REG_3_EN_I_t, Ring_Counter_6, or_2_out, REG3_100);
  and and_11 (REG_4_EN_I_t, Ring_Counter_6, or_2_out, REG4_101);
  and and_12 (OUTPUT_REG_EN_I_t, Ring_Counter_6, or_2_out, OUTPUT_REG_111);
  or or_7 (or_7_out, INSTRUCTION_15, INSTRUCTION_11, INSTRUCTION_16, INSTRUCTION_17, INSTRUCTION_18, INSTRUCTION_19);
  or or_8 (or_8_out, INSTRUCTION_1, INSTRUCTION_3, INSTRUCTION_5, INSTRUCTION_6, INSTRUCTION_7, INSTRUCTION_9, INSTRUCTION_10, INSTRUCTION_14, INSTRUCTION_23);
  and and_13 (PC_RESET_t, ALU_A_I_EN, INSTRUCTION_26);
  or or_9 (or_9_out, INSTRUCTION_12, INSTRUCTION_0, INSTRUCTION_2, INSTRUCTION_4, INSTRUCTION_8, INSTRUCTION_13, INSTRUCTION_20, INSTRUCTION_21, INSTRUCTION_22, INSTRUCTION_26, INSTRUCTION_30);
  and and_14 (and_14_out, or_7_out, Ring_Counter_5);
  and and_15 (and_15_out, or_8_out, Ring_Counter_5);
  Three_State_Output_8bits three_state_output_8bits_1 (.O(BUS_O), .I(Addrs_or_Literal), .EN(and_16_out));
  and and_16 (and_16_out, or_9_out, Ring_Counter_5);
  or or_10 (ALU_EN, and_16_out, and_14_out, and_15_out);
  and and_17 (ACC_EN_BUS_O_t, and_15_out, ACC_000);
  and and_18 (REG_0_EN_O_t, and_15_out, REG0_001);
  and and_19 (REG_1_EN_O_t, and_15_out, REG1_010);
  and and_20 (REG_2_EN_O_t, and_15_out, REG2_011);
  and and_21 (REG_3_EN_O_t, and_15_out, REG3_100);
  and and_22 (REG_4_EN_O_t, and_15_out, REG4_101);
  and and_23 (INPUT_REG_EN_O_t, and_15_out, INPUT_REG_110);
  and and_24 (and_24_out, REG0_001, and_6_out);
  and and_25 (and_25_out, REG1_010, and_6_out);
  and and_26 (and_26_out, REG2_011, and_6_out);
  and and_27 (and_27_out, REG3_100, and_6_out);
  and and_28 (and_28_out, REG4_101, and_6_out);
  and and_29 (and_29_out, OUTPUT_REG_111, and_6_out);
  Decoder #(.enable("false"), .select(5)) decoder_1 (
    .out0(INSTRUCTION_0), .out1(INSTRUCTION_1), .out2(INSTRUCTION_2), .out3(INSTRUCTION_3),
    .out4(INSTRUCTION_4), .out5(INSTRUCTION_5), .out6(INSTRUCTION_6), .out7(INSTRUCTION_7),
    .out8(INSTRUCTION_8), .out9(INSTRUCTION_9), .out10(INSTRUCTION_10), .out11(INSTRUCTION_11),
    .out12(INSTRUCTION_12), .out13(INSTRUCTION_13), .out14(INSTRUCTION_14), .out15(INSTRUCTION_15),
    .out16(INSTRUCTION_16), .out17(INSTRUCTION_17), .out18(INSTRUCTION_18), .out19(INSTRUCTION_19),
    .out20(INSTRUCTION_20), .out21(INSTRUCTION_21), .out22(INSTRUCTION_22), .out23(INSTRUCTION_23),
    .out24(INSTRUCTION_24), .out25(HALT), .out26(INSTRUCTION_26), .out27(INSTRUCTION_27),
    .out28(INSTRUCTION_28), .out29(INSTRUCTION_29), .out30(INSTRUCTION_30), .out31(INSTRUCTION_31),
    .sel(ALU_OPCODE));
  or or_11 (or_11_out, INSTRUCTION_12, INSTRUCTION_0, INSTRUCTION_2, INSTRUCTION_4, INSTRUCTION_8, INSTRUCTION_11, INSTRUCTION_13, INSTRUCTION_15, INSTRUCTION_16, INSTRUCTION_17, INSTRUCTION_18, INSTRUCTION_19, INSTRUCTION_20, INSTRUCTION_30);
  and and_30 (and_30_out, INSTRUCTION_21, ACC_000, Ring_Counter_6);
  and and_31 (and_31_out, or_11_out, Ring_Counter_6);
  and and_32 (and_32_out, INSTRUCTION_21, REG0_001, Ring_Counter_6);
  and and_33 (and_33_out, INSTRUCTION_21, REG1_010, Ring_Counter_6);
  and and_34 (and_34_out, INSTRUCTION_21, REG2_011, Ring_Counter_6);
  and and_35 (and_35_out, INSTRUCTION_21, REG3_100, Ring_Counter_6);
  and and_36 (and_36_out, INSTRUCTION_21, REG4_101, Ring_Counter_6);
  and and_37 (and_37_out, INSTRUCTION_21, INPUT_REG_110, Ring_Counter_6);
  or or_12 (ACC_EN_BUS_O, ACC_EN_BUS_O_t, and_30_out, and_31_out);
  or or_13 (REG_0_EN_I, REG_0_EN_I_t, and_24_out);
  or or_14 (REG_1_EN_I, REG_1_EN_I_t, and_25_out);
  or or_15 (REG_2_EN_I, REG_2_EN_I_t, and_26_out);
  or or_16 (REG_3_EN_I, REG_3_EN_I_t, and_27_out);
  or or_17 (REG_4_EN_I, REG_4_EN_I_t, and_28_out);
  or or_18 (OUTPUT_REG_EN_I, OUTPUT_REG_EN_I_t, and_29_out);
  or or_19 (or_19_out, INSTRUCTION_13, INSTRUCTION_14);
  and and_38 (PC_Load, INSTRUCTION_26, Ring_Counter_5);
  and and_39 (and_39_out, INSTRUCTION_21, Ring_Counter_5);
  and and_40 (and_40_out, Ring_Counter_5, INSTRUCTION_22);
  or or_20 (REG_0_EN_O, and_32_out, REG_0_EN_O_t);
  or or_21 (REG_1_EN_O, and_33_out, REG_1_EN_O_t);
  or or_22 (REG_2_EN_O, and_34_out, REG_2_EN_O_t);
  or or_23 (REG_3_EN_O, and_35_out, REG_3_EN_O_t);
  or or_24 (REG_4_EN_O, and_36_out, REG_4_EN_O_t);
  or or_25 (INPUT_REG_EN_O, and_37_out, INPUT_REG_EN_O_t);
  Decoder #(.enable("false"), .select(3)) decoder_2 (
    .out0(ACC_000), .out1(REG0_001), .out2(REG1_010), .out3(REG2_011), .out4(REG3_100), .out5(REG4_101),
    .out6(INPUT_REG_110), .out7(OUTPUT_REG_111), .sel(Output_Selector));
  and and_41 (ALU_SUBTRACT, or_19_out, Ring_Counter_5);
  or or_26 (MAR_EN, PC_EN_O, and_39_out, and_40_out);
  or or_27 (or_27_out, INSTRUCTION_0, INSTRUCTION_1, INSTRUCTION_2, INSTRUCTION_3, INSTRUCTION_4, INSTRUCTION_5, INSTRUCTION_6, INSTRUCTION_7, INSTRUCTION_8, INSTRUCTION_9, INSTRUCTION_10, INSTRUCTION_11, INSTRUCTION_12, INSTRUCTION_13, INSTRUCTION_14, INSTRUCTION_15, INSTRUCTION_16, INSTRUCTION_17, INSTRUCTION_18, INSTRUCTION_19, INSTRUCTION_23, INSTRUCTION_20);
  or or_28 (Cout_NBout, ALU_SUBTRACT, STATUS_Cout_NBout);
  and and_42 (ACC_EN_I_t, or_27_out, Ring_Counter_5);
  and and_43 (and_43_out, INSTRUCTION_22, Ring_Counter_6);
  and and_44 (and_44_out, INSTRUCTION_21, Ring_Counter_6);
  or or_29 (MDR_EN_I, and_43_out, and_44_out, MDR_EN_I_t);
  and and_45 (and_45_out, Ring_Counter_6, INSTRUCTION_22);
  not not_1 (not_1_out, STATUS_Z);
  or or_30 (MDR_SEL_I, and_45_out, MDR_EN_I_t);
  or or_31 (RAM_EN_O, and_45_out, MDR_EN_I_t);
  and and_46 (and_46_out, Ring_Counter_6, INSTRUCTION_27, STATUS_N);
  and and_47 (and_47_out, Ring_Counter_6, INSTRUCTION_28, STATUS_Z);
  and and_48 (and_48_out, Ring_Counter_6, INSTRUCTION_29, not_1_out);
  or or_32 (PC_Count, and_46_out, and_47_out, and_48_out, ALU_A_I_EN);

  assign ACC_CLR = Master_Reset;
  assign ALU_A_I_CLR = Master_Reset;
  assign IR_CLR = Master_Reset;
  assign MAR_CLR = Master_Reset;
  assign MDR_CLR = Master_Reset;
  assign RAM_CLR = Master_Reset;
  assign RAM_NR_W = MDR_SEL_O;
  assign REG_0_CLR = Master_Reset;
  assign REG_1_CLR = Master_Reset;
  assign REG_2_CLR = Master_Reset;
  assign REG_3_CLR = Master_Reset;
  assign REG_4_CLR = Master_Reset;
  assign STATUS_CLR = Master_Reset;
  assign STATUS_EN = ALU_EN;

  // Other names for the same wires on the sheet: INSTRUCTION_25 = HALT; OPCODE[4:0] = ALU_OPCODE;
  //   OPCODE_0 = ALU_OPCODE[0]; OPCODE_1 = ALU_OPCODE[1]; OPCODE_2 = ALU_OPCODE[2]; OPCODE_3 = ALU_OPCODE[3];
  //   OPCODE_4 = ALU_OPCODE[4]; Upper_B0 = Output_Selector[0]; Upper_B1 = Output_Selector[1];
  //   Upper_B2 = Output_Selector[2]; MAR_EN_t = PC_EN_O; Ring_Counter_0 = PC_EN_O; MDR_SEL_I_t = MDR_EN_I_t;
  //   RAM_EN_I_t = MDR_EN_I_t; RAM_EN_O_t = MDR_EN_I_t; Ring_Counter_1 = MDR_EN_I_t; MDR_EN_O_t = IR_EN_I;
  //   Ring_Counter_2 = IR_EN_I; Ring_Counter_3 = IR_EN_O; PC_COUNT_t = ALU_A_I_EN; Ring_Counter_4 = ALU_A_I_EN
endmodule

module CPU (
  input  [7:0] BUS_UPPER_I,
  input  [7:0] BUS_I,
  input  Master_Reset,
  input  CLK,
  output Output_Port_EN_I,
  output Input_Port_EN_O,
  output MAR_EN,
  output MAR_CLR,
  output RAM_NR_W,
  output RAM_EN_I,
  output RAM_EN_O,
  output RAM_CLR,
  output MDR_SEL_I,
  output MDR_EN_I,
  output MDR_SEL_O,
  output MDR_EN_O,
  output MDR_CLR,
  output HALT,
  output [7:0] BUS_O
);

  wire ACC_CLR, ACC_EN_BUS_O, ACC_EN_I, ACC_SEL_I, ALU_A_I_CLR, ALU_A_I_EN, ALU_ACC_cout_nbout, ALU_ACC_n,
       ALU_ACC_z, ALU_EN, ALU_SUB, Cout_NBout, IR_CLR, IR_EN_I, IR_EN_O, PC_COUNT, PC_EN_O, PC_LOAD,
       PC_RESET, REG_0_CLR, REG_0_EN_I, REG_0_EN_O, REG_1_CLR, REG_1_EN_I, REG_1_EN_O, REG_2_CLR, REG_2_EN_I,
       REG_2_EN_O, REG_3_CLR, REG_3_EN_I, REG_3_EN_O, REG_4_CLR, REG_4_EN_I, REG_4_EN_O, STATUS_CLR,
       STATUS_Cout_NBout, STATUS_EN, STATUS_N, STATUS_Z;
  wire [4:0] ALU_OPCODE;
  wire [7:0] IR_o, IR_o_upper;

  Program_Counter PC (
    .O(BUS_O), .Reset(PC_RESET), .Enable_Output(PC_EN_O), .I(BUS_I), .Load(PC_LOAD), .Count(PC_COUNT),
    .CLK(CLK));
  Instruction_Register IR (
    .O(IR_o), .O_Upper(IR_o_upper), .I(BUS_I), .CLR(IR_CLR), .CLK(CLK), .I_Upper(BUS_UPPER_I),
    .EN_I(IR_EN_I), .EN_O(IR_EN_O));
  Register_8bit_Three_State_Output CPU_REG_0 (
    .O(BUS_O), .I(BUS_I), .CLR(REG_0_CLR), .CLK(CLK), .EN_I(REG_0_EN_I), .EN_O(REG_0_EN_O));
  Register_8bit_Three_State_Output CPU_REG_1 (
    .O(BUS_O), .I(BUS_I), .CLR(REG_1_CLR), .CLK(CLK), .EN_I(REG_1_EN_I), .EN_O(REG_1_EN_O));
  ALU_Accumulator ALU_ACC (
    .BUS_Output(BUS_O), .Z(ALU_ACC_z), .N(ALU_ACC_n), .Cout_NBout(ALU_ACC_cout_nbout),
    .A_I_Enable(ALU_A_I_EN), .A_I_Clear(ALU_A_I_CLR), .Cin_NBin(Cout_NBout), .Subtract(ALU_SUB),
    .ALU_Enable(ALU_EN), .ALU_Op_Select(ALU_OPCODE), .ACC_Select_Input(ACC_SEL_I), .ACC_Clear(ACC_CLR),
    .ACC_Enable_Input(ACC_EN_I), .CLK(CLK), .BUS_Input(BUS_I), .ACC_Enable_BUS_Output(ACC_EN_BUS_O));
  Register_8bit_Three_State_Output CPU_REG_2 (
    .O(BUS_O), .I(BUS_I), .CLR(REG_2_CLR), .CLK(CLK), .EN_I(REG_2_EN_I), .EN_O(REG_2_EN_O));
  Status_Register Status_REG (
    .Cout_NBout_O(STATUS_Cout_NBout), .Z_O(STATUS_Z), .N_O(STATUS_N), .Cout_NBout(ALU_ACC_cout_nbout),
    .Z(ALU_ACC_z), .N(ALU_ACC_n), .Enable(STATUS_EN), .CLK(CLK), .CLR(STATUS_CLR));
  Register_8bit_Three_State_Output CPU_REG_3 (
    .O(BUS_O), .I(BUS_I), .CLR(REG_3_CLR), .CLK(CLK), .EN_I(REG_3_EN_I), .EN_O(REG_3_EN_O));
  Control_Unit control_unit_1 (
    .BUS_O(BUS_O), .IR_EN_I(IR_EN_I), .IR_EN_O(IR_EN_O), .ALU_A_I_EN(ALU_A_I_EN), .PC_EN_O(PC_EN_O),
    .ACC_EN_I(ACC_EN_I), .ACC_SELECT_I(ACC_SEL_I), .RAM_EN_I(RAM_EN_I), .RAM_NR_W(RAM_NR_W),
    .MDR_SEL_O(MDR_SEL_O), .MDR_EN_O(MDR_EN_O), .ALU_OPCODE(ALU_OPCODE), .ALU_EN(ALU_EN),
    .STATUS_EN(STATUS_EN), .REG_0_EN_I(REG_0_EN_I), .REG_1_EN_I(REG_1_EN_I), .REG_2_EN_I(REG_2_EN_I),
    .REG_3_EN_I(REG_3_EN_I), .REG_4_EN_I(REG_4_EN_I), .OUTPUT_REG_EN_I(Output_Port_EN_I), .HALT(HALT),
    .PC_Load(PC_LOAD), .ACC_EN_BUS_O(ACC_EN_BUS_O), .REG_0_EN_O(REG_0_EN_O), .REG_1_EN_O(REG_1_EN_O),
    .REG_2_EN_O(REG_2_EN_O), .REG_3_EN_O(REG_3_EN_O), .REG_4_EN_O(REG_4_EN_O),
    .INPUT_REG_EN_O(Input_Port_EN_O), .MAR_EN(MAR_EN), .ALU_SUBTRACT(ALU_SUB), .Cout_NBout(Cout_NBout),
    .MDR_EN_I(MDR_EN_I), .MDR_SEL_I(MDR_SEL_I), .RAM_EN_O(RAM_EN_O), .PC_Count(PC_COUNT), .MAR_CLR(MAR_CLR),
    .MDR_CLR(MDR_CLR), .RAM_CLR(RAM_CLR), .PC_Reset(PC_RESET), .IR_CLR(IR_CLR), .REG_0_CLR(REG_0_CLR),
    .REG_1_CLR(REG_1_CLR), .REG_2_CLR(REG_2_CLR), .REG_3_CLR(REG_3_CLR), .REG_4_CLR(REG_4_CLR),
    .ALU_A_I_CLR(ALU_A_I_CLR), .ACC_CLR(ACC_CLR), .STATUS_CLR(STATUS_CLR), .CLK(CLK),
    .IR_Upper_I(IR_o_upper), .IR_I(IR_o), .STATUS_Cout_NBout(STATUS_Cout_NBout), .STATUS_N(STATUS_N),
    .STATUS_Z(STATUS_Z), .Master_Reset(Master_Reset));
  Register_8bit_Three_State_Output CPU_REG_4 (
    .O(BUS_O), .I(BUS_I), .CLR(REG_4_CLR), .CLK(CLK), .EN_I(REG_4_EN_I), .EN_O(REG_4_EN_O));
endmodule

module Binary_to_7_Segment_Decoder (
  input  [3:0] I,
  input  NH_L,
  input  dot,
  output a,
  output b,
  output c,
  output decimal,
  output d,
  output e,
  output f,
  output g
);

  wire and_1_out, and_2_out, and_3_out, and_4_out, and_5_out, and_6_out, and_7_out, and_8_out, and_9_out,
       and_10_out, and_11_out, and_12_out, and_13_out, and_14_out, and_15_out, and_16_out, and_17_out,
       and_18_out, and_19_out, and_20_out, and_21_out, and_22_out, and_23_out, and_24_out, and_25_out,
       and_26_out, and_27_out, and_28_out, and_29_out, and_30_out, and_31_out, and_32_out, and_33_out, NA0,
       NA1, NA2, NA3, not_5_out, not_6_out, not_7_out, not_8_out, not_9_out, not_10_out, not_11_out,
       or_1_out, or_2_out, or_3_out, or_4_out, or_5_out, or_6_out, or_7_out;

  not not_1 (NA0, I[0]);
  not not_2 (NA1, I[1]);
  not not_3 (NA2, I[2]);
  not not_4 (NA3, I[3]);
  xor xor_1 (decimal, NH_L, dot);
  and and_1 (and_1_out, NA0, NA2);
  and and_2 (and_2_out, NA3, I[1]);
  and and_3 (and_3_out, NA3, I[2], I[0]);
  and and_4 (and_4_out, I[2], I[1]);
  and and_5 (and_5_out, I[3], NA0);
  and and_6 (and_6_out, I[3], NA2, NA1);
  and and_7 (and_7_out, NA2, NA1, NA0);
  and and_8 (and_8_out, NA2, I[1], I[0]);
  and and_9 (and_9_out, NA3, I[1], NA0);
  and and_10 (and_10_out, I[2], NA1, I[0]);
  and and_11 (and_11_out, I[3], I[2], NA0);
  and and_12 (and_12_out, NA3, I[2]);
  and and_13 (and_13_out, I[3], I[0]);
  and and_14 (and_14_out, I[3], NA2);
  or or_1 (or_1_out, and_1_out, and_2_out, and_3_out, and_4_out, and_5_out, and_6_out);
  or or_2 (or_2_out, and_7_out, and_8_out, and_9_out, and_10_out, and_11_out);
  or or_3 (or_3_out, I[1], and_12_out, and_13_out, and_14_out);
  Multiplexer multiplexer_1 (.in0(or_1_out), .in1(not_5_out), .out(a), .sel(NH_L));
  not not_5 (not_5_out, or_1_out);
  Multiplexer multiplexer_2 (.in0(or_2_out), .in1(not_6_out), .out(d), .sel(NH_L));
  not not_6 (not_6_out, or_2_out);
  Multiplexer multiplexer_3 (.in0(or_3_out), .in1(not_7_out), .out(g), .sel(NH_L));
  not not_7 (not_7_out, or_3_out);
  and and_15 (and_15_out, NA0, NA2);
  and and_16 (and_16_out, NA3, NA2);
  and and_17 (and_17_out, NA3, NA1, NA0);
  and and_18 (and_18_out, NA3, I[1], I[0]);
  and and_19 (and_19_out, I[3], NA1, I[0]);
  and and_20 (and_20_out, NA2, NA0);
  and and_21 (and_21_out, I[1], NA0);
  and and_22 (and_22_out, I[3], I[2]);
  and and_23 (and_23_out, I[3], I[1]);
  or or_4 (or_4_out, and_15_out, and_16_out, and_17_out, and_18_out, and_19_out);
  or or_5 (or_5_out, and_20_out, and_21_out, and_22_out, and_23_out);
  not not_8 (not_8_out, or_4_out);
  not not_9 (not_9_out, or_5_out);
  Multiplexer multiplexer_4 (.in0(or_4_out), .in1(not_8_out), .out(b), .sel(NH_L));
  Multiplexer multiplexer_5 (.in0(or_5_out), .in1(not_9_out), .out(e), .sel(NH_L));
  and and_24 (and_24_out, NA3, NA1);
  and and_25 (and_25_out, NA3, I[0]);
  and and_26 (and_26_out, NA1, I[0]);
  and and_27 (and_27_out, NA3, I[2]);
  and and_28 (and_28_out, I[3], NA2);
  and and_29 (and_29_out, NA1, NA0);
  and and_30 (and_30_out, I[3], NA2);
  and and_31 (and_31_out, I[3], I[1]);
  and and_32 (and_32_out, NA3, I[2], NA0);
  and and_33 (and_33_out, NA3, I[2], NA1);
  or or_6 (or_6_out, and_24_out, and_25_out, and_26_out, and_27_out, and_28_out);
  or or_7 (or_7_out, and_29_out, and_30_out, and_31_out, and_32_out, and_33_out);
  Multiplexer multiplexer_6 (.in0(or_6_out), .in1(not_10_out), .out(c), .sel(NH_L));
  not not_10 (not_10_out, or_6_out);
  Multiplexer multiplexer_7 (.in0(or_7_out), .in1(not_11_out), .out(f), .sel(NH_L));
  not not_11 (not_11_out, or_7_out);

  // Other names for the same wires on the sheet: A0 = I[0]; A1 = I[1]; A2 = I[2]; A3 = I[3]; S = NH_L
endmodule

module Input_Port (
  input  [7:0] I,
  input  CLR,
  input  CLK,
  input  EN_I,
  input  EN_O,
  output [7:0] O
);

  Register_8bit_Three_State_Output register_8bit_three_state_output_1 (
    .O(O), .I(I), .CLR(CLR), .CLK(CLK), .EN_I(EN_I), .EN_O(EN_O));
endmodule

module Output_Port (
  input  [7:0] I,
  input  CLR,
  input  CLK,
  input  EN_I,
  output [6:0] Lower_4bits,
  output [6:0] Upper_4bits
);

  wire [7:0] register_8bit_1_o;

  Register_8bit register_8bit_1 (.O(register_8bit_1_o), .I(I), .Enable(EN_I), .CLK(CLK), .CLR(CLR));
  Binary_to_7_Segment_Decoder binary_to_7_segment_decoder_1 (
    .b(Lower_4bits[1]), .e(Lower_4bits[4]), .c(Lower_4bits[2]), .f(Lower_4bits[5]), .g(Lower_4bits[6]),
    .a(Lower_4bits[0]), .d(Lower_4bits[3]), .I(register_8bit_1_o[3:0]));  // open: decimal, NH_L, dot
  Binary_to_7_Segment_Decoder binary_to_7_segment_decoder_2 (
    .b(Upper_4bits[1]), .e(Upper_4bits[4]), .c(Upper_4bits[2]), .f(Upper_4bits[5]), .g(Upper_4bits[6]),
    .a(Upper_4bits[0]), .d(Upper_4bits[3]), .I(register_8bit_1_o[7:4]));  // open: decimal, NH_L, dot
endmodule

module Ring_Counter_4_States (
  input  CLK,
  input  Reset,
  output Output_0,
  output Output_1,
  output Output_2,
  output Output_3
);

  wire and_1_out, not_1_out, not_2_out, t_ff_1_q, t_ff_1_qn, t_ff_2_q, t_ff_2_qn;

  not not_1 (not_1_out, CLK);
  T_Flip_Flop t_ff_1 (.T(1'b1), .clk(not_1_out), .Q(t_ff_1_q), .Qn(t_ff_1_qn), .reset(Reset));  // open: preset
  T_Flip_Flop t_ff_2 (.T(t_ff_1_q), .clk(not_1_out), .Q(t_ff_2_q), .Qn(t_ff_2_qn), .reset(Reset));  // open: preset
  and and_1 (and_1_out, t_ff_2_qn, t_ff_1_qn);
  not not_2 (not_2_out, Reset);
  and and_2 (Output_0, and_1_out, not_2_out);
  and and_3 (Output_1, t_ff_1_q, t_ff_2_qn);
  and and_4 (Output_2, t_ff_2_q, t_ff_1_qn);
  and and_5 (Output_3, t_ff_2_q, t_ff_1_q);
endmodule

module ROM_to_RAM_Transfer (
  input  MAR_EN,
  input  [15:0] Data_Out,
  input  MDR_EN_I,
  input  MDR_SEL_O,
  input  RAM_NR_W,
  input  RAM_EN_I,
  input  Start_Transfer,
  input  CLK,
  input  RAM_CLR,
  input  MAR_CLR,
  input  MDR_CLR,
  input  CLR_RAM,
  output [7:0] Lower_BUS,
  output [7:0] Addrs,
  output MAR_EN_T,
  output [7:0] Upper_BUS,
  output MDR_EN_I_T,
  output MDR_SEL_O_T,
  output RAM_NR_W_T,
  output TO_MASTER_RST_ROM,
  output RAM_EN_I_T,
  output RAM_CLR_T,
  output MAR_CLR_T,
  output MDR_CLR_T
);

  wire EN_ADDRS_OUT, MDR_EN_I_ROM, MDR_SEL_O_ROM, not_1_out, or_1_out, RING_COUNTER_4;

  Program_Counter program_counter_1 (
    .O(Addrs), .Reset(not_1_out), .Enable_Output(1'b1), .Count(RING_COUNTER_4), .CLK(CLK));  // open: I, Load
  Three_State_Output_8bits three_state_output_8bits_1 (.O(Lower_BUS), .I(Addrs), .EN(EN_ADDRS_OUT));
  not not_1 (not_1_out, Start_Transfer);
  Ring_Counter_4_States ring_counter_4_states_1 (
    .Output_0(EN_ADDRS_OUT), .Output_1(MDR_EN_I_ROM), .Output_2(MDR_SEL_O_ROM), .Output_3(RING_COUNTER_4),
    .CLK(CLK), .Reset(not_1_out));
  and and_1 (RAM_CLR_T, not_1_out, CLR_RAM, RAM_CLR);
  and and_2 (MAR_CLR_T, not_1_out, CLR_RAM, MAR_CLR);
  and and_3 (MDR_CLR_T, not_1_out, CLR_RAM, MDR_CLR);
  Three_State_Output_8bits three_state_output_8bits_2 (.O(Lower_BUS), .I(Data_Out[7:0]), .EN(or_1_out));
  Three_State_Output_8bits three_state_output_8bits_3 (.O(Upper_BUS), .I(Data_Out[15:8]), .EN(or_1_out));
  or or_1 (or_1_out, MDR_SEL_O_ROM, MDR_EN_I_ROM);
  or or_2 (MAR_EN_T, MAR_EN, EN_ADDRS_OUT);
  or or_3 (MDR_EN_I_T, MDR_EN_I, MDR_EN_I_ROM);
  or or_4 (MDR_SEL_O_T, MDR_SEL_O, MDR_SEL_O_ROM);
  or or_5 (RAM_NR_W_T, RAM_NR_W, MDR_SEL_O_ROM);
  or or_6 (RAM_EN_I_T, RAM_EN_I, MDR_SEL_O_ROM);

  assign TO_MASTER_RST_ROM = Start_Transfer;

  // Other names for the same wires on the sheet: MAR_EN_ROM = EN_ADDRS_OUT; RAM_EN_I_ROM = MDR_SEL_O_ROM;
  //   RAM_NR_W_ROM = MDR_SEL_O_ROM
endmodule
module Computer (
  input  Master_Reset,
  input  [7:0] Input_Data,
  input  EN_Input_Data,
  input  CLEAR_RAM_MDR_MAR,
  input  Start_Transfer
);

  wire a0, a1, b0, b1, c0, c1, CLK, CLK_out, d0, d1, e0, e1, f0, f1, g0, g1, HALT, Input_Port_EN_O, MAR_CLR,
       MAR_CLR_T, MAR_EN, MAR_EN_T, Master_Reset_ROM, Master_Reset_t, MDR_CLR, MDR_CLR_T, MDR_EN_I,
       MDR_EN_I_T, MDR_EN_O, MDR_SEL_I, MDR_SEL_O, MDR_SEL_O_T, not_1_out, Output_Port_EN_I, RAM_CLR,
       RAM_CLR_T, RAM_EN_I, RAM_EN_I_T, RAM_EN_O, RAM_NR_W, RAM_NR_W_T;
  wire [7:0] BUS_Lower_8bits, BUS_Upper_8bits, rom_to_ram_transfer_1_addrs;
  wire [15:0] rom_1_data;

  or or_1 (Master_Reset_t, Master_Reset, Master_Reset_ROM);
  Input_Port input_port_1 (
    .O(BUS_Lower_8bits), .I(Input_Data), .CLR(Master_Reset_t), .CLK(CLK), .EN_I(EN_Input_Data),
    .EN_O(Input_Port_EN_O));
  CPU cpu_1 (
    .BUS_O(BUS_Lower_8bits), .Input_Port_EN_O(Input_Port_EN_O), .HALT(HALT),
    .Output_Port_EN_I(Output_Port_EN_I), .MAR_EN(MAR_EN), .MAR_CLR(MAR_CLR), .RAM_NR_W(RAM_NR_W),
    .RAM_EN_I(RAM_EN_I), .RAM_EN_O(RAM_EN_O), .RAM_CLR(RAM_CLR), .MDR_SEL_I(MDR_SEL_I), .MDR_EN_I(MDR_EN_I),
    .MDR_SEL_O(MDR_SEL_O), .MDR_EN_O(MDR_EN_O), .MDR_CLR(MDR_CLR), .BUS_UPPER_I(BUS_Upper_8bits),
    .BUS_I(BUS_Lower_8bits), .Master_Reset(Master_Reset_t), .CLK(CLK));
  Clock u_CLK (.out(CLK_out));
  not not_1 (not_1_out, HALT);
  and and_1 (CLK, CLK_out, not_1_out);
  Output_Port output_port_1 (
    .Lower_4bits({g0, f0, e0, d0, c0, b0, a0}), .Upper_4bits({g1, f1, e1, d1, c1, b1, a1}),
    .I(BUS_Lower_8bits), .CLR(Master_Reset_t), .CLK(CLK), .EN_I(Output_Port_EN_I));
  RAM_MAR_MDR ram_mar_mdr_1 (
    .BUS_O_Upper(BUS_Upper_8bits), .BUS_O(BUS_Lower_8bits), .Select_MDR_I(MDR_SEL_I),
    .Select_MDR_O(MDR_SEL_O_T), .EN_MDR_I(MDR_EN_I_T), .EN_MDR_O(MDR_EN_O), .CLR_MDR(MDR_CLR_T),
    .BUS_I(BUS_Lower_8bits), .CLK(CLK), .EN_MAR(MAR_EN_T), .CLR_MAR(MAR_CLR_T), .NR_W_RAM(RAM_NR_W_T),
    .EN_RAM_I(RAM_EN_I_T), .EN_RAM_O(RAM_EN_O), .Upper_BUS_I(BUS_Upper_8bits), .CLR_RAM(RAM_CLR_T));
  ROM #(.dataWidth(16)) rom_1 (.addr(rom_to_ram_transfer_1_addrs), .data(rom_1_data));
  ROM_to_RAM_Transfer rom_to_ram_transfer_1 (
    .RAM_CLR_T(RAM_CLR_T), .MAR_CLR_T(MAR_CLR_T), .MDR_CLR_T(MDR_CLR_T), .Lower_BUS(BUS_Lower_8bits),
    .Upper_BUS(BUS_Upper_8bits), .RAM_EN_I_T(RAM_EN_I_T), .MAR_EN_T(MAR_EN_T), .MDR_EN_I_T(MDR_EN_I_T),
    .MDR_SEL_O_T(MDR_SEL_O_T), .RAM_NR_W_T(RAM_NR_W_T), .Addrs(rom_to_ram_transfer_1_addrs),
    .TO_MASTER_RST_ROM(Master_Reset_ROM), .RAM_CLR(RAM_CLR), .MAR_CLR(MAR_CLR), .MDR_CLR(MDR_CLR),
    .CLR_RAM(CLEAR_RAM_MDR_MAR), .Data_Out(rom_1_data), .RAM_EN_I(RAM_EN_I), .MAR_EN(MAR_EN),
    .MDR_EN_I(MDR_EN_I), .MDR_SEL_O(MDR_SEL_O), .RAM_NR_W(RAM_NR_W), .Start_Transfer(Start_Transfer),
    .CLK(CLK));
  _7_Segment_Display u_7_segment_display_1 (.g(g1), .f(f1), .a(a1), .b(b1), .e(e1), .d(d1), .c(c1));  // open: dp
  _7_Segment_Display u_7_segment_display_2 (.g(g0), .f(f0), .a(a0), .b(b0), .e(e0), .d(d0), .c(c0));  // open: dp

  // Other names for the same wires on the sheet: CLR_RAM_MDR_MAR = CLEAR_RAM_MDR_MAR; MASTER_RST = Master_Reset
endmodule
